// Logisim project ALU.circ as structural Verilog: 9 circuits, main circuit main
module main (
  input  X3,
  input  X2,
  input  X1,
  input  X0,
  input  Y3,
  input  Y2,
  input  Y1,
  input  Y0,
  input  S3,
  input  S2,
  input  S1,
  input  S0,
  output Cout,
  output G3,
  output G2,
  output G1,
  output G0
);

  ALU alu_1 (
    .X3(X3), .X2(X2), .X1(X1), .X0(X0), .Y3(Y3), .Y2(Y2), .Y1(Y1), .Y0(Y0), .S3(S3), .S2(S2), .S1(S1),
    .S0(S0), .Cout(Cout), .G3(G3), .G2(G2), .G1(G1), .G0(G0));

  // Notes on the sheet:
  //   ALU
endmodule

module _4_bit_adder (
  input  Cin,
  input  B0,
  input  A0,
  input  B1,
  input  A1,
  input  B2,
  input  A2,
  input  B3,
  input  A3,
  output S0,
  output S1,
  output S2,
  output S3,
  output cout
);

  wire adder_1_cout, adder_2_cout, adder_3_cout;

  Adder #(.width(1)) adder_1 (.a(B0), .b(A0), .out(S0), .cin(Cin), .cout(adder_1_cout));
  Adder #(.width(1)) adder_2 (.a(B1), .b(A1), .out(S1), .cin(adder_1_cout), .cout(adder_2_cout));
  Adder #(.width(1)) adder_3 (.a(B2), .b(A2), .out(S2), .cin(adder_2_cout), .cout(adder_3_cout));
  Adder #(.width(1)) adder_4 (.a(B3), .b(A3), .out(S3), .cin(adder_3_cout), .cout(cout));
endmodule

module _4_bit_adder__without_input_logic_for_subtraction (
  input  X3,
  input  X2,
  input  X1,
  input  X0,
  input  S_Cin,
  input  Y3,
  input  Y2,
  input  Y1,
  input  Y0,
  output G3,
  output G2,
  output G1,
  output G0,
  output Cout
);

  _4_bit_adder u_4_bit_adder_1 (
    .Cin(S_Cin), .B0(X0), .A0(Y0), .B1(X1), .A1(Y1), .B2(X2), .A2(Y2), .B3(X3), .A3(Y3), .S0(G0), .S1(G1),
    .S2(G2), .S3(G3), .cout(Cout));
endmodule

module Adder__2_ssubtractor (
  input  X3,
  input  X2,
  input  X1,
  input  X0,
  input  S_Cin,
  input  Y3,
  input  Y2,
  input  Y1,
  input  Y0,
  output G3,
  output G2,
  output G1,
  output G0,
  output Cout
);

  wire xor_1_out, xor_2_out, xor_3_out, xor_4_out;

  xor xor_1 (xor_1_out, Y3, S_Cin);
  xor xor_2 (xor_2_out, Y2, S_Cin);
  xor xor_3 (xor_3_out, Y1, S_Cin);
  xor xor_4 (xor_4_out, Y0, S_Cin);
  _4_bit_adder u_4_bit_adder_1 (
    .Cin(S_Cin), .B0(X0), .A0(xor_4_out), .B1(X1), .A1(xor_3_out), .B2(X2), .A2(xor_2_out), .B3(X3),
    .A3(xor_1_out), .S0(G0), .S1(G1), .S2(G2), .S3(G3), .cout(Cout));
endmodule

module _4x1_MUX (
  input  in_1,
  input  in_2,
  input  in_3,
  input  in_4,
  input  S1,
  input  S0,
  output G
);

  wire and_1_out, and_2_out, and_3_out, and_4_out, and_5_out, and_6_out, and_7_out, and_8_out, not_1_out,
       not_2_out, not_3_out, not_4_out;

  and and_1 (and_1_out, not_2_out, not_1_out);
  not not_1 (not_1_out, S0);
  not not_2 (not_2_out, S1);
  not not_3 (not_3_out, S1);
  and and_2 (and_2_out, S1, not_4_out);
  and and_3 (and_3_out, not_3_out, S0);
  not not_4 (not_4_out, S0);
  and and_4 (and_4_out, in_1, and_1_out);
  and and_5 (and_5_out, in_2, and_3_out);
  and and_6 (and_6_out, in_3, and_2_out);
  and and_7 (and_7_out, in_4, and_8_out);
  and and_8 (and_8_out, S0, S1);
  or or_1 (G, and_4_out, and_5_out, and_6_out, and_7_out);
endmodule

module Quad_2x1_Mux_Control_input (
  input  A3,
  input  L3,
  input  A2,
  input  L2,
  input  A1,
  input  L1,
  input  A0,
  input  L0,
  input  S,
  output _03,
  output _02,
  output _01,
  output O0
);

  wire undriven;

  Multiplexer multiplexer_1 (.in0(A2), .in1(L2), .out(_02), .sel(S));  // open: en
  Multiplexer multiplexer_2 (.in0(A1), .in1(L1), .out(_01), .sel(S));  // open: en
  Multiplexer multiplexer_3 (.in0(A0), .in1(L0), .out(O0), .sel(S));  // open: en
  Multiplexer multiplexer_4 (.in0(A3), .in1(L3), .out(_03), .sel(S), .en(undriven));
endmodule

module Arithmetic_unit (
  input  X3,
  input  X2,
  input  X1,
  input  X0,
  input  Y3,
  input  Y2,
  input  Y1,
  input  Y0,
  input  S2,
  input  S1,
  input  S0,
  output G3,
  output G2,
  output G1,
  output G0,
  output Cout
);

  wire and_1_out, and_2_out, and_3_out, and_4_out, and_5_out, and_6_out, and_7_out, and_8_out, not_1_out,
       not_2_out, not_3_out, not_4_out, or_1_out, or_2_out, or_3_out, or_4_out;

  not not_1 (not_1_out, Y3);
  not not_2 (not_2_out, Y2);
  not not_3 (not_3_out, Y1);
  not not_4 (not_4_out, Y0);
  and and_1 (and_1_out, not_1_out, S2);
  and and_2 (and_2_out, Y3, S1);
  and and_3 (and_3_out, not_2_out, S2);
  and and_4 (and_4_out, Y2, S1);
  and and_5 (and_5_out, not_3_out, S2);
  and and_6 (and_6_out, Y1, S1);
  and and_7 (and_7_out, not_4_out, S2);
  and and_8 (and_8_out, Y0, S1);
  or or_1 (or_1_out, and_1_out, and_2_out);
  or or_2 (or_2_out, and_3_out, and_4_out);
  or or_3 (or_3_out, and_5_out, and_6_out);
  or or_4 (or_4_out, and_7_out, and_8_out);
  _4_bit_adder__without_input_logic_for_subtraction u_4_bit_adder_without_input_logic_for_subtraction_1 (
    .S_Cin(S0), .Y3(or_1_out), .Y2(or_2_out), .Y1(or_3_out), .Y0(or_4_out), .X3(X3), .X2(X2), .X1(X1),
    .X0(X0), .G3(G3), .G2(G2), .G1(G1), .G0(G0), .Cout(Cout));
endmodule

module Logic_Unit (
  input  X3,
  input  Y3,
  input  X2,
  input  Y2,
  input  X1,
  input  Y1,
  input  X0,
  input  Y0,
  input  S0,
  input  in_10,
  output G3,
  output G2,
  output G1,
  output G0
);

  wire and_1_out, and_2_out, and_3_out, and_4_out, not_1_out, not_2_out, not_3_out, not_4_out, or_1_out,
       or_2_out, or_3_out, or_4_out, xor_1_out, xor_2_out, xor_3_out, xor_4_out;

  and and_1 (and_1_out, X3, Y3);
  or or_1 (or_1_out, X3, Y3);
  xor xor_1 (xor_1_out, X3, Y3);
  not not_1 (not_1_out, X3);
  and and_2 (and_2_out, X2, Y2);
  or or_2 (or_2_out, X2, Y2);
  xor xor_2 (xor_2_out, X2, Y2);
  not not_2 (not_2_out, X2);
  and and_3 (and_3_out, X1, Y1);
  or or_3 (or_3_out, X1, Y1);
  xor xor_3 (xor_3_out, X1, Y1);
  not not_3 (not_3_out, X1);
  and and_4 (and_4_out, X0, Y0);
  or or_4 (or_4_out, X0, Y0);
  xor xor_4 (xor_4_out, X0, Y0);
  not not_4 (not_4_out, X0);
  _4x1_MUX u_4x1_mux_1 (
    .in_1(and_1_out), .in_2(or_1_out), .in_3(xor_1_out), .in_4(not_1_out), .S1(S0), .S0(in_10), .G(G3));
  _4x1_MUX u_4x1_mux_2 (
    .in_1(and_2_out), .in_2(or_2_out), .in_3(xor_2_out), .in_4(not_2_out), .S1(S0), .S0(in_10), .G(G2));
  _4x1_MUX u_4x1_mux_3 (
    .in_1(and_3_out), .in_2(or_3_out), .in_3(xor_3_out), .in_4(not_3_out), .S1(S0), .S0(in_10), .G(G1));
  _4x1_MUX u_4x1_mux_4 (
    .in_1(and_4_out), .in_2(or_4_out), .in_3(xor_4_out), .in_4(not_4_out), .S1(S0), .S0(in_10), .G(G0));
endmodule

module ALU (
  input  X3,
  input  X2,
  input  X1,
  input  X0,
  input  Y3,
  input  Y2,
  input  Y1,
  input  Y0,
  input  S3,
  input  S2,
  input  S1,
  input  S0,
  output Cout,
  output G3,
  output G2,
  output G1,
  output G0
);

  wire arithmetic_unit_1_g0, arithmetic_unit_1_g1, arithmetic_unit_1_g2, arithmetic_unit_1_g3,
       logic_unit_1_g0, logic_unit_1_g1, logic_unit_1_g2, logic_unit_1_g3;

  Arithmetic_unit arithmetic_unit_1 (
    .Y3(Y3), .Y2(Y2), .Y1(Y1), .Y0(Y0), .X3(X3), .X2(X2), .X1(X1), .X0(X0), .S2(S2), .S1(S1), .S0(S0),
    .G3(arithmetic_unit_1_g3), .G2(arithmetic_unit_1_g2), .G1(arithmetic_unit_1_g1),
    .G0(arithmetic_unit_1_g0), .Cout(Cout));
  Logic_Unit logic_unit_1 (
    .X3(X3), .X2(X2), .X1(X1), .X0(X0), .Y3(Y3), .Y2(Y2), .Y1(Y1), .Y0(Y0), .S0(S0), .in_10(S1),
    .G3(logic_unit_1_g3), .G2(logic_unit_1_g2), .G1(logic_unit_1_g1), .G0(logic_unit_1_g0));
  Quad_2x1_Mux_Control_input quad_2x1_mux_control_input_1 (
    .A3(arithmetic_unit_1_g3), .L3(logic_unit_1_g3), .A2(arithmetic_unit_1_g2), .L2(logic_unit_1_g2),
    .A1(arithmetic_unit_1_g1), .L1(logic_unit_1_g1), .A0(arithmetic_unit_1_g0), .L0(logic_unit_1_g0), .S(S3),
    ._03(G3), ._02(G2), ._01(G1), .O0(G0));
endmodule
