// Logisim project Data Path.circ as structural Verilog: 10 circuits, main circuit main
module main (
);

  DATA_PATH data_path_1 ();  // open: Write, DA, AA, Read_Write, _0___ALU___1___RAM, Uin3, Uin2, Uin1, Uin0, S3, S2, S1, S0, Cout, G3, G2, G1, G0, BA, User_Input
endmodule

module _4bit_adder___Arithmetic_unit_Subcircuit (
  input  Cin,
  input  B0,
  input  A0,
  input  B1,
  input  A1,
  input  B2,
  input  A2,
  input  B3,
  input  A3,
  output S0,
  output S1,
  output S2,
  output S3,
  output cout
);

  wire adder_1_cout, adder_2_cout, adder_3_cout;

  Adder #(.width(1)) adder_1 (.a(B0), .b(A0), .out(S0), .cin(Cin), .cout(adder_1_cout));
  Adder #(.width(1)) adder_2 (.a(B1), .b(A1), .out(S1), .cin(adder_1_cout), .cout(adder_2_cout));
  Adder #(.width(1)) adder_3 (.a(B2), .b(A2), .out(S2), .cin(adder_2_cout), .cout(adder_3_cout));
  Adder #(.width(1)) adder_4 (.a(B3), .b(A3), .out(S3), .cin(adder_3_cout), .cout(cout));
endmodule

module Quad_2x1_Set_of_Mux (
  input  A3,
  input  A2,
  input  A1,
  input  A0,
  input  L3,
  input  L2,
  input  L1,
  input  L0,
  input  S,
  output _03,
  output _02,
  output _01,
  output O0
);

  wire undriven;

  Multiplexer multiplexer_1 (.in0(A0), .in1(L0), .out(O0), .sel(S));  // open: en
  Multiplexer multiplexer_2 (.in0(A3), .in1(L3), .out(_03), .sel(S), .en(undriven));
  Multiplexer multiplexer_3 (.in0(A2), .in1(L2), .out(_02), .sel(S));  // open: en
  Multiplexer multiplexer_4 (.in0(A1), .in1(L1), .out(_01), .sel(S));  // open: en
endmodule

module Arithmetic_unit___ALU_subcircuit (
  input  X3,
  input  X2,
  input  X1,
  input  X0,
  input  Y3,
  input  Y2,
  input  Y1,
  input  Y0,
  input  S2,
  input  S1,
  input  S0,
  output G3,
  output G2,
  output G1,
  output G0,
  output Cout
);

  wire and_1_out, and_2_out, and_3_out, and_4_out, and_5_out, and_6_out, and_7_out, and_8_out, not_1_out,
       not_2_out, not_3_out, not_4_out, or_1_out, or_2_out, or_3_out, or_4_out;

  not not_1 (not_1_out, Y3);
  not not_2 (not_2_out, Y2);
  not not_3 (not_3_out, Y1);
  not not_4 (not_4_out, Y0);
  and and_1 (and_1_out, not_1_out, S2);
  and and_2 (and_2_out, Y3, S1);
  and and_3 (and_3_out, not_2_out, S2);
  and and_4 (and_4_out, Y2, S1);
  and and_5 (and_5_out, not_3_out, S2);
  and and_6 (and_6_out, Y1, S1);
  and and_7 (and_7_out, not_4_out, S2);
  and and_8 (and_8_out, Y0, S1);
  or or_1 (or_1_out, and_1_out, and_2_out);
  or or_2 (or_2_out, and_3_out, and_4_out);
  or or_3 (or_3_out, and_5_out, and_6_out);
  or or_4 (or_4_out, and_7_out, and_8_out);
  _4bit_adder___Arithmetic_unit_Subcircuit u_4bit_adder_arithmetic_unit_subcircuit_1 (
    .Cin(S0), .B0(X0), .A0(or_1_out), .B1(X1), .A1(or_2_out), .B2(X2), .A2(or_3_out), .B3(X3), .A3(or_4_out),
    .S0(G0), .S1(G1), .S2(G2), .S3(G3), .cout(Cout));

  // Notes on the sheet:
  //   4-Bit
  //   Adder
endmodule

module Logic_Unit___ALU_subcircuit (
  input  X3,
  input  Y3,
  input  X2,
  input  Y2,
  input  X1,
  input  Y1,
  input  X0,
  input  Y0,
  input  S0,
  input  S1,
  output G3,
  output G2,
  output G1,
  output G0
);

  wire and_1_out, and_2_out, and_3_out, and_4_out, not_1_out, not_2_out, not_3_out, not_4_out, or_1_out,
       or_2_out, or_3_out, or_4_out, xor_1_out, xor_2_out, xor_3_out, xor_4_out;

  and and_1 (and_1_out, X3, Y3);
  or or_1 (or_1_out, X3, Y3);
  not not_1 (not_1_out, X3);
  and and_2 (and_2_out, X2, Y2);
  or or_2 (or_2_out, X2, Y2);
  not not_2 (not_2_out, X2);
  and and_3 (and_3_out, X1, Y1);
  or or_3 (or_3_out, X1, Y1);
  not not_3 (not_3_out, X1);
  and and_4 (and_4_out, X0, Y0);
  or or_4 (or_4_out, X0, Y0);
  not not_4 (not_4_out, X0);
  xor xor_1 (xor_1_out, X3, Y3);
  xor xor_2 (xor_2_out, X2, Y2);
  xor xor_3 (xor_3_out, X1, Y1);
  xor xor_4 (xor_4_out, X0, Y0);
  Multiplexer #(.select(2)) multiplexer_1 (
    .in0(and_1_out), .in1(xor_1_out), .in2(or_1_out), .in3(not_1_out), .out(G3), .sel({S1, S0}));  // open: en
  Multiplexer #(.select(2)) multiplexer_2 (
    .in0(and_2_out), .in1(xor_2_out), .in2(or_2_out), .in3(not_2_out), .out(G2), .sel({S1, S0}));  // open: en
  Multiplexer #(.select(2)) multiplexer_3 (
    .in0(and_3_out), .in1(xor_3_out), .in2(or_3_out), .in3(not_3_out), .out(G1), .sel({S1, S0}));  // open: en
  Multiplexer #(.select(2)) multiplexer_4 (
    .in0(and_4_out), .in1(xor_4_out), .in2(or_4_out), .in3(not_4_out), .out(G0), .sel({S1, S0}));  // open: en
endmodule

module ALU (
  input  X3,
  input  X2,
  input  X1,
  input  X0,
  input  Y3,
  input  Y2,
  input  Y1,
  input  Y0,
  input  S3,
  input  S2,
  input  S1,
  input  S0,
  output Cout,
  output G3,
  output G2,
  output G1,
  output G0
);

  wire arithmetic_unit_alu_subcircuit_1_g0, arithmetic_unit_alu_subcircuit_1_g1,
       arithmetic_unit_alu_subcircuit_1_g2, arithmetic_unit_alu_subcircuit_1_g3,
       logic_unit_alu_subcircuit_1_g0, logic_unit_alu_subcircuit_1_g1, logic_unit_alu_subcircuit_1_g2,
       logic_unit_alu_subcircuit_1_g3;

  Arithmetic_unit___ALU_subcircuit arithmetic_unit_alu_subcircuit_1 (
    .Y3(Y3), .Y2(Y2), .Y1(Y1), .Y0(Y0), .X3(X3), .X2(X2), .X1(X1), .X0(X0), .S2(S2), .S1(S1), .S0(S0),
    .G3(arithmetic_unit_alu_subcircuit_1_g3), .G2(arithmetic_unit_alu_subcircuit_1_g2),
    .G1(arithmetic_unit_alu_subcircuit_1_g1), .G0(arithmetic_unit_alu_subcircuit_1_g0), .Cout(Cout));
  Logic_Unit___ALU_subcircuit logic_unit_alu_subcircuit_1 (
    .X3(X3), .X2(X2), .X1(X1), .X0(X0), .Y3(Y3), .Y2(Y2), .Y1(Y1), .Y0(Y0), .S0(S0), .S1(S1),
    .G3(logic_unit_alu_subcircuit_1_g3), .G2(logic_unit_alu_subcircuit_1_g2),
    .G1(logic_unit_alu_subcircuit_1_g1), .G0(logic_unit_alu_subcircuit_1_g0));
  Quad_2x1_Set_of_Mux quad_2x1_set_of_mux_1 (
    .A3(arithmetic_unit_alu_subcircuit_1_g3), .A2(arithmetic_unit_alu_subcircuit_1_g2),
    .A1(arithmetic_unit_alu_subcircuit_1_g1), .A0(arithmetic_unit_alu_subcircuit_1_g0),
    .L3(logic_unit_alu_subcircuit_1_g3), .L2(logic_unit_alu_subcircuit_1_g2),
    .L1(logic_unit_alu_subcircuit_1_g1), .L0(logic_unit_alu_subcircuit_1_g0), .S(S3), ._03(G3), ._02(G2),
    ._01(G1), .O0(G0));

  // Notes on the sheet:
  //   Arithmetic Unit
  //   LogicUnit
  //   2x1
  //   Control 
  //   Mux
endmodule

module _4x8_register_File (
  input  D3,
  input  D2,
  input  D1,
  input  D0,
  input  WRITE,
  input  [2:0] DA,
  input  [2:0] BA,
  input  [2:0] AA,
  output A3,
  output A2,
  output A1,
  output A0,
  output B3,
  output B2,
  output B1,
  output B0
);

  wire clock_1_out, decoder_1_out0, decoder_1_out1, decoder_1_out2, decoder_1_out3, decoder_1_out4,
       decoder_1_out5, decoder_1_out6, decoder_1_out7;
  wire [3:0] R0_q, R1_q, R2_q, R3_q, R4_q, R5_q, R6_q, R7_q;

  Decoder #(.select(3)) decoder_1 (
    .out0(decoder_1_out0), .out1(decoder_1_out1), .out2(decoder_1_out2), .out3(decoder_1_out3),
    .out4(decoder_1_out4), .out5(decoder_1_out5), .out6(decoder_1_out6), .out7(decoder_1_out7), .sel(DA),
    .en(WRITE));
  Register #(.width(4)) R0 (.D({D3, D2, D1, D0}), .en(decoder_1_out0), .Q(R0_q), .clk(clock_1_out));  // open: clr
  Register #(.width(4)) R2 (.D({D3, D2, D1, D0}), .en(decoder_1_out2), .Q(R2_q), .clk(clock_1_out));  // open: clr
  Register #(.width(4)) R4 (.D({D3, D2, D1, D0}), .en(decoder_1_out4), .Q(R4_q), .clk(clock_1_out));  // open: clr
  Register #(.width(4)) R6 (.D({D3, D2, D1, D0}), .en(decoder_1_out6), .Q(R6_q), .clk(clock_1_out));  // open: clr
  Clock clock_1 (.out(clock_1_out));
  Register #(.width(4)) R1 (.D({D3, D2, D1, D0}), .en(decoder_1_out1), .Q(R1_q), .clk(clock_1_out));  // open: clr
  Register #(.width(4)) R3 (.D({D3, D2, D1, D0}), .en(decoder_1_out3), .Q(R3_q), .clk(clock_1_out));  // open: clr
  Register #(.width(4)) R5 (.D({D3, D2, D1, D0}), .en(decoder_1_out5), .Q(R5_q), .clk(clock_1_out));  // open: clr
  Register #(.width(4)) R7 (.D({D3, D2, D1, D0}), .en(decoder_1_out7), .Q(R7_q), .clk(clock_1_out));  // open: clr
  Multiplexer #(.select(3)) multiplexer_1 (
    .in0(R0_q[3]), .in1(R1_q[3]), .in2(R2_q[3]), .in3(R3_q[3]), .in4(R4_q[3]), .in5(R5_q[3]), .in6(R6_q[3]),
    .in7(R7_q[3]), .out(A3), .sel(AA));  // open: en
  Multiplexer #(.select(3)) multiplexer_2 (
    .in0(R0_q[2]), .in1(R1_q[2]), .in2(R2_q[2]), .in3(R3_q[2]), .in4(R4_q[2]), .in5(R5_q[2]), .in6(R6_q[2]),
    .in7(R7_q[2]), .out(A2), .sel(AA));  // open: en
  Multiplexer #(.select(3)) multiplexer_3 (
    .in0(R0_q[1]), .in1(R1_q[1]), .in2(R2_q[1]), .in3(R3_q[1]), .in4(R4_q[1]), .in5(R5_q[1]), .in6(R6_q[1]),
    .in7(R7_q[1]), .out(A1), .sel(AA));  // open: en
  Multiplexer #(.select(3)) multiplexer_4 (
    .in0(R0_q[0]), .in1(R1_q[0]), .in2(R2_q[0]), .in3(R3_q[0]), .in4(R4_q[0]), .in5(R5_q[0]), .in6(R6_q[0]),
    .in7(R7_q[0]), .out(A0), .sel(AA));  // open: en
  Multiplexer #(.select(3)) multiplexer_5 (
    .in0(R0_q[3]), .in1(R1_q[3]), .in2(R2_q[3]), .in3(R3_q[3]), .in4(R4_q[3]), .in5(R5_q[3]), .in6(R6_q[3]),
    .in7(R7_q[3]), .out(B3), .sel(BA));  // open: en
  Multiplexer #(.select(3)) multiplexer_6 (
    .in0(R0_q[2]), .in1(R1_q[2]), .in2(R2_q[2]), .in3(R3_q[2]), .in4(R4_q[2]), .in5(R5_q[2]), .in6(R6_q[2]),
    .in7(R7_q[2]), .out(B2), .sel(BA));  // open: en
  Multiplexer #(.select(3)) multiplexer_7 (
    .in0(R0_q[1]), .in1(R1_q[1]), .in2(R2_q[1]), .in3(R3_q[1]), .in4(R4_q[1]), .in5(R5_q[1]), .in6(R6_q[1]),
    .in7(R7_q[1]), .out(B1), .sel(BA));  // open: en
  Multiplexer #(.select(3)) multiplexer_8 (
    .in0(R0_q[0]), .in1(R1_q[0]), .in2(R2_q[0]), .in3(R3_q[0]), .in4(R4_q[0]), .in5(R5_q[0]), .in6(R6_q[0]),
    .in7(R7_q[0]), .out(B0), .sel(BA));  // open: en
endmodule

module Binary_cell___RAM_subcircuit (
  input  Select,
  input  Input,
  input  Read_Write,
  output Output
);

  wire and_1_out, and_2_out, clock_1_out, not_1_out, not_2_out, s_r_ff_1_q;

  not not_1 (not_1_out, Input);
  and and_1 (and_1_out, Select, not_1_out, not_2_out);
  and and_2 (and_2_out, Select, Input, not_2_out);
  Clock clock_1 (.out(clock_1_out));
  not not_2 (not_2_out, Read_Write);
  S_R_Flip_Flop s_r_ff_1 (
    .S(and_2_out), .clk(clock_1_out), .R(and_1_out), .Q(s_r_ff_1_q));  // open: Qn, preset, reset, en
  and and_3 (Output, Select, s_r_ff_1_q, Read_Write);
endmodule

module _16x4_RAM (
  input  I3,
  input  I2,
  input  I1,
  input  I0,
  input  RAM_select,
  input  [3:0] Address,
  input  Read_Write,
  output O3,
  output O2,
  output O1,
  output O0
);

  wire binary_cell_ram_subcircuit_1_output, binary_cell_ram_subcircuit_2_output,
       binary_cell_ram_subcircuit_3_output, binary_cell_ram_subcircuit_4_output,
       binary_cell_ram_subcircuit_5_output, binary_cell_ram_subcircuit_6_output,
       binary_cell_ram_subcircuit_7_output, binary_cell_ram_subcircuit_8_output,
       binary_cell_ram_subcircuit_9_output, binary_cell_ram_subcircuit_10_output,
       binary_cell_ram_subcircuit_11_output, binary_cell_ram_subcircuit_12_output,
       binary_cell_ram_subcircuit_13_output, binary_cell_ram_subcircuit_14_output,
       binary_cell_ram_subcircuit_15_output, binary_cell_ram_subcircuit_16_output,
       binary_cell_ram_subcircuit_17_output, binary_cell_ram_subcircuit_18_output,
       binary_cell_ram_subcircuit_19_output, binary_cell_ram_subcircuit_20_output,
       binary_cell_ram_subcircuit_21_output, binary_cell_ram_subcircuit_22_output,
       binary_cell_ram_subcircuit_23_output, binary_cell_ram_subcircuit_24_output,
       binary_cell_ram_subcircuit_25_output, binary_cell_ram_subcircuit_26_output,
       binary_cell_ram_subcircuit_27_output, binary_cell_ram_subcircuit_28_output,
       binary_cell_ram_subcircuit_29_output, binary_cell_ram_subcircuit_30_output,
       binary_cell_ram_subcircuit_31_output, binary_cell_ram_subcircuit_32_output,
       binary_cell_ram_subcircuit_33_output, binary_cell_ram_subcircuit_34_output,
       binary_cell_ram_subcircuit_35_output, binary_cell_ram_subcircuit_36_output,
       binary_cell_ram_subcircuit_37_output, binary_cell_ram_subcircuit_38_output,
       binary_cell_ram_subcircuit_39_output, binary_cell_ram_subcircuit_40_output,
       binary_cell_ram_subcircuit_41_output, binary_cell_ram_subcircuit_42_output,
       binary_cell_ram_subcircuit_43_output, binary_cell_ram_subcircuit_44_output,
       binary_cell_ram_subcircuit_45_output, binary_cell_ram_subcircuit_46_output,
       binary_cell_ram_subcircuit_47_output, binary_cell_ram_subcircuit_48_output,
       binary_cell_ram_subcircuit_49_output, binary_cell_ram_subcircuit_50_output,
       binary_cell_ram_subcircuit_51_output, binary_cell_ram_subcircuit_52_output,
       binary_cell_ram_subcircuit_53_output, binary_cell_ram_subcircuit_54_output,
       binary_cell_ram_subcircuit_55_output, binary_cell_ram_subcircuit_56_output,
       binary_cell_ram_subcircuit_57_output, binary_cell_ram_subcircuit_58_output,
       binary_cell_ram_subcircuit_59_output, binary_cell_ram_subcircuit_60_output,
       binary_cell_ram_subcircuit_61_output, binary_cell_ram_subcircuit_62_output,
       binary_cell_ram_subcircuit_63_output, binary_cell_ram_subcircuit_64_output, decoder_1_out0,
       decoder_1_out1, decoder_1_out2, decoder_1_out3, decoder_1_out4, decoder_1_out5, decoder_1_out6,
       decoder_1_out7, decoder_1_out8, decoder_1_out9, decoder_1_out10, decoder_1_out11, decoder_1_out12,
       decoder_1_out13, decoder_1_out14, decoder_1_out15;

  Decoder #(.select(4)) decoder_1 (
    .out0(decoder_1_out0), .out1(decoder_1_out1), .out2(decoder_1_out2), .out3(decoder_1_out3),
    .out4(decoder_1_out4), .out5(decoder_1_out5), .out6(decoder_1_out6), .out7(decoder_1_out7),
    .out8(decoder_1_out8), .out9(decoder_1_out9), .out10(decoder_1_out10), .out11(decoder_1_out11),
    .out12(decoder_1_out12), .out13(decoder_1_out13), .out14(decoder_1_out14), .out15(decoder_1_out15),
    .sel(Address), .en(RAM_select));
  Binary_cell___RAM_subcircuit binary_cell_ram_subcircuit_1 (
    .Input(I3), .Select(decoder_1_out0), .Read_Write(Read_Write), .Output(binary_cell_ram_subcircuit_1_output));
  Binary_cell___RAM_subcircuit binary_cell_ram_subcircuit_2 (
    .Input(I3), .Select(decoder_1_out1), .Read_Write(Read_Write), .Output(binary_cell_ram_subcircuit_2_output));
  Binary_cell___RAM_subcircuit binary_cell_ram_subcircuit_3 (
    .Input(I3), .Select(decoder_1_out2), .Read_Write(Read_Write), .Output(binary_cell_ram_subcircuit_3_output));
  Binary_cell___RAM_subcircuit binary_cell_ram_subcircuit_4 (
    .Input(I3), .Select(decoder_1_out3), .Read_Write(Read_Write), .Output(binary_cell_ram_subcircuit_4_output));
  Binary_cell___RAM_subcircuit binary_cell_ram_subcircuit_5 (
    .Input(I3), .Select(decoder_1_out4), .Read_Write(Read_Write), .Output(binary_cell_ram_subcircuit_5_output));
  Binary_cell___RAM_subcircuit binary_cell_ram_subcircuit_6 (
    .Input(I3), .Select(decoder_1_out5), .Read_Write(Read_Write), .Output(binary_cell_ram_subcircuit_6_output));
  Binary_cell___RAM_subcircuit binary_cell_ram_subcircuit_7 (
    .Input(I3), .Select(decoder_1_out6), .Read_Write(Read_Write), .Output(binary_cell_ram_subcircuit_7_output));
  Binary_cell___RAM_subcircuit binary_cell_ram_subcircuit_8 (
    .Input(I3), .Select(decoder_1_out7), .Read_Write(Read_Write), .Output(binary_cell_ram_subcircuit_8_output));
  Binary_cell___RAM_subcircuit binary_cell_ram_subcircuit_9 (
    .Input(I3), .Select(decoder_1_out8), .Read_Write(Read_Write), .Output(binary_cell_ram_subcircuit_9_output));
  Binary_cell___RAM_subcircuit binary_cell_ram_subcircuit_10 (
    .Input(I3), .Select(decoder_1_out9), .Read_Write(Read_Write),
    .Output(binary_cell_ram_subcircuit_10_output));
  Binary_cell___RAM_subcircuit binary_cell_ram_subcircuit_11 (
    .Input(I3), .Select(decoder_1_out10), .Read_Write(Read_Write),
    .Output(binary_cell_ram_subcircuit_11_output));
  Binary_cell___RAM_subcircuit binary_cell_ram_subcircuit_12 (
    .Input(I3), .Select(decoder_1_out11), .Read_Write(Read_Write),
    .Output(binary_cell_ram_subcircuit_12_output));
  Binary_cell___RAM_subcircuit binary_cell_ram_subcircuit_13 (
    .Input(I3), .Select(decoder_1_out12), .Read_Write(Read_Write),
    .Output(binary_cell_ram_subcircuit_13_output));
  Binary_cell___RAM_subcircuit binary_cell_ram_subcircuit_14 (
    .Input(I3), .Select(decoder_1_out13), .Read_Write(Read_Write),
    .Output(binary_cell_ram_subcircuit_14_output));
  Binary_cell___RAM_subcircuit binary_cell_ram_subcircuit_15 (
    .Input(I3), .Select(decoder_1_out14), .Read_Write(Read_Write),
    .Output(binary_cell_ram_subcircuit_15_output));
  Binary_cell___RAM_subcircuit binary_cell_ram_subcircuit_16 (
    .Input(I3), .Select(decoder_1_out15), .Read_Write(Read_Write),
    .Output(binary_cell_ram_subcircuit_16_output));
  or or_1 (O3, binary_cell_ram_subcircuit_16_output, binary_cell_ram_subcircuit_15_output, binary_cell_ram_subcircuit_14_output, binary_cell_ram_subcircuit_13_output, binary_cell_ram_subcircuit_12_output, binary_cell_ram_subcircuit_11_output, binary_cell_ram_subcircuit_10_output, binary_cell_ram_subcircuit_9_output, binary_cell_ram_subcircuit_8_output, binary_cell_ram_subcircuit_7_output, binary_cell_ram_subcircuit_6_output, binary_cell_ram_subcircuit_5_output, binary_cell_ram_subcircuit_4_output, binary_cell_ram_subcircuit_3_output, binary_cell_ram_subcircuit_2_output, binary_cell_ram_subcircuit_1_output);
  Binary_cell___RAM_subcircuit binary_cell_ram_subcircuit_17 (
    .Input(I2), .Select(decoder_1_out0), .Read_Write(Read_Write),
    .Output(binary_cell_ram_subcircuit_17_output));
  Binary_cell___RAM_subcircuit binary_cell_ram_subcircuit_18 (
    .Input(I2), .Select(decoder_1_out1), .Read_Write(Read_Write),
    .Output(binary_cell_ram_subcircuit_18_output));
  Binary_cell___RAM_subcircuit binary_cell_ram_subcircuit_19 (
    .Input(I2), .Select(decoder_1_out2), .Read_Write(Read_Write),
    .Output(binary_cell_ram_subcircuit_19_output));
  Binary_cell___RAM_subcircuit binary_cell_ram_subcircuit_20 (
    .Input(I2), .Select(decoder_1_out3), .Read_Write(Read_Write),
    .Output(binary_cell_ram_subcircuit_20_output));
  Binary_cell___RAM_subcircuit binary_cell_ram_subcircuit_21 (
    .Input(I2), .Select(decoder_1_out4), .Read_Write(Read_Write),
    .Output(binary_cell_ram_subcircuit_21_output));
  Binary_cell___RAM_subcircuit binary_cell_ram_subcircuit_22 (
    .Input(I2), .Select(decoder_1_out5), .Read_Write(Read_Write),
    .Output(binary_cell_ram_subcircuit_22_output));
  Binary_cell___RAM_subcircuit binary_cell_ram_subcircuit_23 (
    .Input(I2), .Select(decoder_1_out6), .Read_Write(Read_Write),
    .Output(binary_cell_ram_subcircuit_23_output));
  Binary_cell___RAM_subcircuit binary_cell_ram_subcircuit_24 (
    .Input(I2), .Select(decoder_1_out7), .Read_Write(Read_Write),
    .Output(binary_cell_ram_subcircuit_24_output));
  Binary_cell___RAM_subcircuit binary_cell_ram_subcircuit_25 (
    .Input(I2), .Select(decoder_1_out8), .Read_Write(Read_Write),
    .Output(binary_cell_ram_subcircuit_25_output));
  Binary_cell___RAM_subcircuit binary_cell_ram_subcircuit_26 (
    .Input(I2), .Select(decoder_1_out9), .Read_Write(Read_Write),
    .Output(binary_cell_ram_subcircuit_26_output));
  Binary_cell___RAM_subcircuit binary_cell_ram_subcircuit_27 (
    .Input(I2), .Select(decoder_1_out10), .Read_Write(Read_Write),
    .Output(binary_cell_ram_subcircuit_27_output));
  Binary_cell___RAM_subcircuit binary_cell_ram_subcircuit_28 (
    .Input(I2), .Select(decoder_1_out11), .Read_Write(Read_Write),
    .Output(binary_cell_ram_subcircuit_28_output));
  Binary_cell___RAM_subcircuit binary_cell_ram_subcircuit_29 (
    .Input(I2), .Select(decoder_1_out12), .Read_Write(Read_Write),
    .Output(binary_cell_ram_subcircuit_29_output));
  Binary_cell___RAM_subcircuit binary_cell_ram_subcircuit_30 (
    .Input(I2), .Select(decoder_1_out13), .Read_Write(Read_Write),
    .Output(binary_cell_ram_subcircuit_30_output));
  Binary_cell___RAM_subcircuit binary_cell_ram_subcircuit_31 (
    .Input(I2), .Select(decoder_1_out14), .Read_Write(Read_Write),
    .Output(binary_cell_ram_subcircuit_31_output));
  Binary_cell___RAM_subcircuit binary_cell_ram_subcircuit_32 (
    .Input(I2), .Select(decoder_1_out15), .Read_Write(Read_Write),
    .Output(binary_cell_ram_subcircuit_32_output));
  or or_2 (O2, binary_cell_ram_subcircuit_32_output, binary_cell_ram_subcircuit_31_output, binary_cell_ram_subcircuit_30_output, binary_cell_ram_subcircuit_29_output, binary_cell_ram_subcircuit_28_output, binary_cell_ram_subcircuit_27_output, binary_cell_ram_subcircuit_26_output, binary_cell_ram_subcircuit_25_output, binary_cell_ram_subcircuit_24_output, binary_cell_ram_subcircuit_23_output, binary_cell_ram_subcircuit_22_output, binary_cell_ram_subcircuit_21_output, binary_cell_ram_subcircuit_20_output, binary_cell_ram_subcircuit_19_output, binary_cell_ram_subcircuit_18_output, binary_cell_ram_subcircuit_17_output);
  Binary_cell___RAM_subcircuit binary_cell_ram_subcircuit_33 (
    .Input(I1), .Select(decoder_1_out0), .Read_Write(Read_Write),
    .Output(binary_cell_ram_subcircuit_33_output));
  Binary_cell___RAM_subcircuit binary_cell_ram_subcircuit_34 (
    .Input(I1), .Select(decoder_1_out1), .Read_Write(Read_Write),
    .Output(binary_cell_ram_subcircuit_34_output));
  Binary_cell___RAM_subcircuit binary_cell_ram_subcircuit_35 (
    .Input(I1), .Select(decoder_1_out2), .Read_Write(Read_Write),
    .Output(binary_cell_ram_subcircuit_35_output));
  Binary_cell___RAM_subcircuit binary_cell_ram_subcircuit_36 (
    .Input(I1), .Select(decoder_1_out3), .Read_Write(Read_Write),
    .Output(binary_cell_ram_subcircuit_36_output));
  Binary_cell___RAM_subcircuit binary_cell_ram_subcircuit_37 (
    .Input(I1), .Select(decoder_1_out4), .Read_Write(Read_Write),
    .Output(binary_cell_ram_subcircuit_37_output));
  Binary_cell___RAM_subcircuit binary_cell_ram_subcircuit_38 (
    .Input(I1), .Select(decoder_1_out5), .Read_Write(Read_Write),
    .Output(binary_cell_ram_subcircuit_38_output));
  Binary_cell___RAM_subcircuit binary_cell_ram_subcircuit_39 (
    .Input(I1), .Select(decoder_1_out6), .Read_Write(Read_Write),
    .Output(binary_cell_ram_subcircuit_39_output));
  Binary_cell___RAM_subcircuit binary_cell_ram_subcircuit_40 (
    .Input(I1), .Select(decoder_1_out7), .Read_Write(Read_Write),
    .Output(binary_cell_ram_subcircuit_40_output));
  Binary_cell___RAM_subcircuit binary_cell_ram_subcircuit_41 (
    .Input(I1), .Select(decoder_1_out8), .Read_Write(Read_Write),
    .Output(binary_cell_ram_subcircuit_41_output));
  Binary_cell___RAM_subcircuit binary_cell_ram_subcircuit_42 (
    .Input(I1), .Select(decoder_1_out9), .Read_Write(Read_Write),
    .Output(binary_cell_ram_subcircuit_42_output));
  Binary_cell___RAM_subcircuit binary_cell_ram_subcircuit_43 (
    .Input(I1), .Select(decoder_1_out10), .Read_Write(Read_Write),
    .Output(binary_cell_ram_subcircuit_43_output));
  Binary_cell___RAM_subcircuit binary_cell_ram_subcircuit_44 (
    .Input(I1), .Select(decoder_1_out11), .Read_Write(Read_Write),
    .Output(binary_cell_ram_subcircuit_44_output));
  Binary_cell___RAM_subcircuit binary_cell_ram_subcircuit_45 (
    .Input(I1), .Select(decoder_1_out12), .Read_Write(Read_Write),
    .Output(binary_cell_ram_subcircuit_45_output));
  Binary_cell___RAM_subcircuit binary_cell_ram_subcircuit_46 (
    .Input(I1), .Select(decoder_1_out13), .Read_Write(Read_Write),
    .Output(binary_cell_ram_subcircuit_46_output));
  Binary_cell___RAM_subcircuit binary_cell_ram_subcircuit_47 (
    .Input(I1), .Select(decoder_1_out14), .Read_Write(Read_Write),
    .Output(binary_cell_ram_subcircuit_47_output));
  Binary_cell___RAM_subcircuit binary_cell_ram_subcircuit_48 (
    .Input(I1), .Select(decoder_1_out15), .Read_Write(Read_Write),
    .Output(binary_cell_ram_subcircuit_48_output));
  or or_3 (O1, binary_cell_ram_subcircuit_48_output, binary_cell_ram_subcircuit_47_output, binary_cell_ram_subcircuit_46_output, binary_cell_ram_subcircuit_45_output, binary_cell_ram_subcircuit_44_output, binary_cell_ram_subcircuit_43_output, binary_cell_ram_subcircuit_42_output, binary_cell_ram_subcircuit_41_output, binary_cell_ram_subcircuit_40_output, binary_cell_ram_subcircuit_39_output, binary_cell_ram_subcircuit_38_output, binary_cell_ram_subcircuit_37_output, binary_cell_ram_subcircuit_36_output, binary_cell_ram_subcircuit_35_output, binary_cell_ram_subcircuit_34_output, binary_cell_ram_subcircuit_33_output);
  Binary_cell___RAM_subcircuit binary_cell_ram_subcircuit_49 (
    .Input(I0), .Select(decoder_1_out0), .Read_Write(Read_Write),
    .Output(binary_cell_ram_subcircuit_49_output));
  Binary_cell___RAM_subcircuit binary_cell_ram_subcircuit_50 (
    .Input(I0), .Select(decoder_1_out1), .Read_Write(Read_Write),
    .Output(binary_cell_ram_subcircuit_50_output));
  Binary_cell___RAM_subcircuit binary_cell_ram_subcircuit_51 (
    .Input(I0), .Select(decoder_1_out2), .Read_Write(Read_Write),
    .Output(binary_cell_ram_subcircuit_51_output));
  Binary_cell___RAM_subcircuit binary_cell_ram_subcircuit_52 (
    .Input(I0), .Select(decoder_1_out3), .Read_Write(Read_Write),
    .Output(binary_cell_ram_subcircuit_52_output));
  Binary_cell___RAM_subcircuit binary_cell_ram_subcircuit_53 (
    .Input(I0), .Select(decoder_1_out4), .Read_Write(Read_Write),
    .Output(binary_cell_ram_subcircuit_53_output));
  Binary_cell___RAM_subcircuit binary_cell_ram_subcircuit_54 (
    .Input(I0), .Select(decoder_1_out5), .Read_Write(Read_Write),
    .Output(binary_cell_ram_subcircuit_54_output));
  Binary_cell___RAM_subcircuit binary_cell_ram_subcircuit_55 (
    .Input(I0), .Select(decoder_1_out6), .Read_Write(Read_Write),
    .Output(binary_cell_ram_subcircuit_55_output));
  Binary_cell___RAM_subcircuit binary_cell_ram_subcircuit_56 (
    .Input(I0), .Select(decoder_1_out7), .Read_Write(Read_Write),
    .Output(binary_cell_ram_subcircuit_56_output));
  Binary_cell___RAM_subcircuit binary_cell_ram_subcircuit_57 (
    .Input(I0), .Select(decoder_1_out8), .Read_Write(Read_Write),
    .Output(binary_cell_ram_subcircuit_57_output));
  Binary_cell___RAM_subcircuit binary_cell_ram_subcircuit_58 (
    .Input(I0), .Select(decoder_1_out9), .Read_Write(Read_Write),
    .Output(binary_cell_ram_subcircuit_58_output));
  Binary_cell___RAM_subcircuit binary_cell_ram_subcircuit_59 (
    .Input(I0), .Select(decoder_1_out10), .Read_Write(Read_Write),
    .Output(binary_cell_ram_subcircuit_59_output));
  Binary_cell___RAM_subcircuit binary_cell_ram_subcircuit_60 (
    .Input(I0), .Select(decoder_1_out11), .Read_Write(Read_Write),
    .Output(binary_cell_ram_subcircuit_60_output));
  Binary_cell___RAM_subcircuit binary_cell_ram_subcircuit_61 (
    .Input(I0), .Select(decoder_1_out12), .Read_Write(Read_Write),
    .Output(binary_cell_ram_subcircuit_61_output));
  Binary_cell___RAM_subcircuit binary_cell_ram_subcircuit_62 (
    .Input(I0), .Select(decoder_1_out13), .Read_Write(Read_Write),
    .Output(binary_cell_ram_subcircuit_62_output));
  Binary_cell___RAM_subcircuit binary_cell_ram_subcircuit_63 (
    .Input(I0), .Select(decoder_1_out14), .Read_Write(Read_Write),
    .Output(binary_cell_ram_subcircuit_63_output));
  Binary_cell___RAM_subcircuit binary_cell_ram_subcircuit_64 (
    .Input(I0), .Select(decoder_1_out15), .Read_Write(Read_Write),
    .Output(binary_cell_ram_subcircuit_64_output));
  or or_4 (O0, binary_cell_ram_subcircuit_64_output, binary_cell_ram_subcircuit_63_output, binary_cell_ram_subcircuit_62_output, binary_cell_ram_subcircuit_61_output, binary_cell_ram_subcircuit_60_output, binary_cell_ram_subcircuit_59_output, binary_cell_ram_subcircuit_58_output, binary_cell_ram_subcircuit_57_output, binary_cell_ram_subcircuit_56_output, binary_cell_ram_subcircuit_55_output, binary_cell_ram_subcircuit_54_output, binary_cell_ram_subcircuit_53_output, binary_cell_ram_subcircuit_52_output, binary_cell_ram_subcircuit_51_output, binary_cell_ram_subcircuit_50_output, binary_cell_ram_subcircuit_49_output);
endmodule

module DATA_PATH (
  input  Write,
  input  [2:0] DA,
  input  [2:0] AA,
  input  [2:0] BA,
  input  User_Input,
  input  Uin3,
  input  Uin2,
  input  Uin1,
  input  Uin0,
  input  Read_Write,
  input  S3,
  input  S2,
  input  S1,
  input  S0,
  input  _0___ALU___1___RAM,
  output Cout,
  output G3,
  output G2,
  output G1,
  output G0
);

  wire n4x8_register_file_1_b0, n4x8_register_file_1_b1, n4x8_register_file_1_b2, n4x8_register_file_1_b3,
       n16x4_ram_1_o0, n16x4_ram_1_o1, n16x4_ram_1_o2, n16x4_ram_1_o3, quad_2x1_set_of_mux_1__01,
       quad_2x1_set_of_mux_1__02, quad_2x1_set_of_mux_1__03, quad_2x1_set_of_mux_1_o0,
       quad_2x1_set_of_mux_2__01, quad_2x1_set_of_mux_2__02, quad_2x1_set_of_mux_2__03,
       quad_2x1_set_of_mux_2_o0;
  wire [3:0] n4x8_register_file_1_a0;

  Quad_2x1_Set_of_Mux quad_2x1_set_of_mux_1 (
    .A3(quad_2x1_set_of_mux_2__03), .A2(quad_2x1_set_of_mux_2__02), .A1(quad_2x1_set_of_mux_2__01),
    .A0(quad_2x1_set_of_mux_2_o0), .L3(Uin3), .L2(Uin2), .L1(Uin1), .L0(Uin0), .S(User_Input),
    ._03(quad_2x1_set_of_mux_1__03), ._02(quad_2x1_set_of_mux_1__02), ._01(quad_2x1_set_of_mux_1__01),
    .O0(quad_2x1_set_of_mux_1_o0));
  Quad_2x1_Set_of_Mux quad_2x1_set_of_mux_2 (
    .A3(G3), .A2(G2), .A1(G1), .A0(G0), .L3(n16x4_ram_1_o3), .L2(n16x4_ram_1_o2), .L1(n16x4_ram_1_o1),
    .L0(n16x4_ram_1_o0), .S(_0___ALU___1___RAM), ._03(quad_2x1_set_of_mux_2__03),
    ._02(quad_2x1_set_of_mux_2__02), ._01(quad_2x1_set_of_mux_2__01), .O0(quad_2x1_set_of_mux_2_o0));
  _4x8_register_File u_4x8_register_file_1 (
    .WRITE(Write), .DA(DA), .AA(AA), .D3(quad_2x1_set_of_mux_1__03), .D2(quad_2x1_set_of_mux_1__02),
    .D1(quad_2x1_set_of_mux_1__01), .D0(quad_2x1_set_of_mux_1_o0), .A3(n4x8_register_file_1_a0[3]),
    .A2(n4x8_register_file_1_a0[2]), .A1(n4x8_register_file_1_a0[1]), .A0(n4x8_register_file_1_a0[0]),
    .B3(n4x8_register_file_1_b3), .B2(n4x8_register_file_1_b2), .B1(n4x8_register_file_1_b1),
    .B0(n4x8_register_file_1_b0), .BA(BA));
  ALU alu_1 (
    .X3(n4x8_register_file_1_a0[3]), .X2(n4x8_register_file_1_a0[2]), .X1(n4x8_register_file_1_a0[1]),
    .X0(n4x8_register_file_1_a0[0]), .Y3(n4x8_register_file_1_b3), .Y2(n4x8_register_file_1_b2),
    .Y1(n4x8_register_file_1_b1), .Y0(n4x8_register_file_1_b0), .S3(S3), .S2(S2), .S1(S1), .S0(S0),
    .Cout(Cout), .G3(G3), .G2(G2), .G1(G1), .G0(G0));
  _16x4_RAM u_16x4_ram_1 (
    .RAM_select(1'b1), .Address(n4x8_register_file_1_a0), .Read_Write(Read_Write),
    .I3(n4x8_register_file_1_b3), .I2(n4x8_register_file_1_b2), .I1(n4x8_register_file_1_b1),
    .I0(n4x8_register_file_1_b0), .O3(n16x4_ram_1_o3), .O2(n16x4_ram_1_o2), .O1(n16x4_ram_1_o1),
    .O0(n16x4_ram_1_o0));
endmodule
