// Logisim project 231488347_lab02_circuit.circ as structural Verilog: 4 circuits, main circuit main
module main (
  input  in_1,
  input  in_2,
  input  in_3,
  input  in_4,
  input  in_5,
  input  in_6,
  input  in_7,
  input  in_8,
  input  in_9,
  output out_10,
  output out_11,
  output out_12,
  output out_13
);

  Ram_8x4 ram_8x4_1 (
    .in_8(in_8), .in_5(in_7), .in_6(in_6), .in_7(in_5), .in_1(in_1), .in_2(in_2), .in_3(in_3), .in_4(in_4),
    .in_9(in_9), .out_10(out_10), .out_11(out_11), .out_12(out_12), .out_13(out_13));
endmodule

module Binary_Cell (
  input  Select,
  input  Input,
  input  Read_Write,
  output out_4
);

  wire and_1_out, and_2_out, clock_out, not_1_out, not_2_out, s_r_ff_1_q;

  not not_1 (not_1_out, Input);
  and and_1 (and_1_out, Select, not_1_out, not_2_out);
  and and_2 (and_2_out, Select, Input, not_2_out);
  Clock clock (.out(clock_out));
  S_R_Flip_Flop s_r_ff_1 (
    .S(and_1_out), .clk(clock_out), .R(and_2_out), .Q(s_r_ff_1_q));  // open: Qn, preset, reset, en
  not not_2 (not_2_out, Read_Write);
  and and_3 (out_4, Select, s_r_ff_1_q, Read_Write);
endmodule

module Decoder (
  input  ENABLE,
  input  in_2,
  input  in_3,
  input  in_4,
  output out_5,
  output out_6,
  output out_7,
  output out_8,
  output out_9,
  output out_10,
  output out_11,
  output out_12
);

  wire not_1_out, not_2_out, not_3_out;

  not not_1 (not_1_out, in_2);
  not not_2 (not_2_out, in_3);
  not not_3 (not_3_out, in_4);
  and and_1 (out_5, not_2_out, not_1_out, not_3_out, ENABLE);
  and and_2 (out_6, not_1_out, not_2_out, in_4, ENABLE);
  and and_3 (out_7, not_1_out, in_3, not_3_out, ENABLE);
  and and_4 (out_8, not_1_out, in_3, in_4, ENABLE);
  and and_5 (out_9, in_2, not_2_out, not_3_out, ENABLE);
  and and_6 (out_10, in_2, not_2_out, in_4, ENABLE);
  and and_7 (out_11, in_2, in_3, not_3_out, ENABLE);
  and and_8 (out_12, in_2, in_3, in_4, ENABLE);
endmodule

module Ram_8x4 (
  input  in_1,
  input  in_2,
  input  in_3,
  input  in_4,
  input  in_5,
  input  in_6,
  input  in_7,
  input  in_8,
  input  in_9,
  output out_10,
  output out_11,
  output out_12,
  output out_13
);

  wire binary_cell_1_out_4, binary_cell_2_out_4, binary_cell_3_out_4, binary_cell_4_out_4,
       binary_cell_5_out_4, binary_cell_6_out_4, binary_cell_7_out_4, binary_cell_8_out_4,
       binary_cell_9_out_4, binary_cell_10_out_4, binary_cell_11_out_4, binary_cell_12_out_4,
       binary_cell_13_out_4, binary_cell_14_out_4, binary_cell_15_out_4, binary_cell_16_out_4,
       binary_cell_17_out_4, binary_cell_18_out_4, binary_cell_19_out_4, binary_cell_20_out_4,
       binary_cell_21_out_4, binary_cell_22_out_4, binary_cell_23_out_4, binary_cell_24_out_4,
       binary_cell_25_out_4, binary_cell_26_out_4, binary_cell_27_out_4, binary_cell_28_out_4,
       binary_cell_29_out_4, binary_cell_30_out_4, binary_cell_31_out_4, binary_cell_32_out_4,
       decoder_1_out_5, decoder_1_out_6, decoder_1_out_7, decoder_1_out_8, decoder_1_out_9, decoder_1_out_10,
       decoder_1_out_11, decoder_1_out_12;

  Decoder decoder_1 (
    .ENABLE(in_8), .in_2(in_5), .in_3(in_6), .in_4(in_7), .out_5(decoder_1_out_5), .out_6(decoder_1_out_6),
    .out_7(decoder_1_out_7), .out_8(decoder_1_out_8), .out_9(decoder_1_out_9), .out_10(decoder_1_out_10),
    .out_11(decoder_1_out_11), .out_12(decoder_1_out_12));
  Binary_Cell binary_cell_1 (.Input(in_1), .Select(decoder_1_out_12), .Read_Write(in_9), .out_4(binary_cell_1_out_4));
  Binary_Cell binary_cell_2 (.Input(in_1), .Select(decoder_1_out_11), .Read_Write(in_9), .out_4(binary_cell_2_out_4));
  Binary_Cell binary_cell_3 (.Input(in_1), .Select(decoder_1_out_10), .Read_Write(in_9), .out_4(binary_cell_3_out_4));
  Binary_Cell binary_cell_4 (.Input(in_1), .Select(decoder_1_out_9), .Read_Write(in_9), .out_4(binary_cell_4_out_4));
  Binary_Cell binary_cell_5 (.Input(in_1), .Select(decoder_1_out_8), .Read_Write(in_9), .out_4(binary_cell_5_out_4));
  Binary_Cell binary_cell_6 (.Input(in_1), .Select(decoder_1_out_7), .Read_Write(in_9), .out_4(binary_cell_6_out_4));
  Binary_Cell binary_cell_7 (.Input(in_1), .Select(decoder_1_out_6), .Read_Write(in_9), .out_4(binary_cell_7_out_4));
  Binary_Cell binary_cell_8 (.Input(in_1), .Select(decoder_1_out_5), .Read_Write(in_9), .out_4(binary_cell_8_out_4));
  or or_1 (out_10, binary_cell_8_out_4, binary_cell_7_out_4, binary_cell_6_out_4, binary_cell_5_out_4, binary_cell_4_out_4, binary_cell_3_out_4, binary_cell_2_out_4, binary_cell_1_out_4);
  Binary_Cell binary_cell_9 (.Input(in_2), .Select(decoder_1_out_12), .Read_Write(in_9), .out_4(binary_cell_9_out_4));
  Binary_Cell binary_cell_10 (.Input(in_2), .Select(decoder_1_out_11), .Read_Write(in_9), .out_4(binary_cell_10_out_4));
  Binary_Cell binary_cell_11 (.Input(in_2), .Select(decoder_1_out_10), .Read_Write(in_9), .out_4(binary_cell_11_out_4));
  Binary_Cell binary_cell_12 (.Input(in_2), .Select(decoder_1_out_9), .Read_Write(in_9), .out_4(binary_cell_12_out_4));
  Binary_Cell binary_cell_13 (.Input(in_2), .Select(decoder_1_out_8), .Read_Write(in_9), .out_4(binary_cell_13_out_4));
  Binary_Cell binary_cell_14 (.Input(in_2), .Select(decoder_1_out_7), .Read_Write(in_9), .out_4(binary_cell_14_out_4));
  Binary_Cell binary_cell_15 (.Input(in_2), .Select(decoder_1_out_6), .Read_Write(in_9), .out_4(binary_cell_15_out_4));
  Binary_Cell binary_cell_16 (.Input(in_2), .Select(decoder_1_out_5), .Read_Write(in_9), .out_4(binary_cell_16_out_4));
  or or_2 (out_11, binary_cell_16_out_4, binary_cell_15_out_4, binary_cell_14_out_4, binary_cell_13_out_4, binary_cell_12_out_4, binary_cell_11_out_4, binary_cell_10_out_4, binary_cell_9_out_4);
  Binary_Cell binary_cell_17 (.Input(in_3), .Select(decoder_1_out_12), .Read_Write(in_9), .out_4(binary_cell_17_out_4));
  Binary_Cell binary_cell_18 (.Input(in_3), .Select(decoder_1_out_11), .Read_Write(in_9), .out_4(binary_cell_18_out_4));
  Binary_Cell binary_cell_19 (.Input(in_3), .Select(decoder_1_out_10), .Read_Write(in_9), .out_4(binary_cell_19_out_4));
  Binary_Cell binary_cell_20 (.Input(in_3), .Select(decoder_1_out_9), .Read_Write(in_9), .out_4(binary_cell_20_out_4));
  Binary_Cell binary_cell_21 (.Input(in_3), .Select(decoder_1_out_8), .Read_Write(in_9), .out_4(binary_cell_21_out_4));
  Binary_Cell binary_cell_22 (.Input(in_3), .Select(decoder_1_out_7), .Read_Write(in_9), .out_4(binary_cell_22_out_4));
  Binary_Cell binary_cell_23 (.Input(in_3), .Select(decoder_1_out_6), .Read_Write(in_9), .out_4(binary_cell_23_out_4));
  Binary_Cell binary_cell_24 (.Input(in_3), .Select(decoder_1_out_5), .Read_Write(in_9), .out_4(binary_cell_24_out_4));
  or or_3 (out_12, binary_cell_24_out_4, binary_cell_23_out_4, binary_cell_22_out_4, binary_cell_21_out_4, binary_cell_20_out_4, binary_cell_19_out_4, binary_cell_18_out_4, binary_cell_17_out_4);
  Binary_Cell binary_cell_25 (.Input(in_4), .Select(decoder_1_out_12), .Read_Write(in_9), .out_4(binary_cell_25_out_4));
  Binary_Cell binary_cell_26 (.Input(in_4), .Select(decoder_1_out_11), .Read_Write(in_9), .out_4(binary_cell_26_out_4));
  Binary_Cell binary_cell_27 (.Input(in_4), .Select(decoder_1_out_10), .Read_Write(in_9), .out_4(binary_cell_27_out_4));
  Binary_Cell binary_cell_28 (.Input(in_4), .Select(decoder_1_out_9), .Read_Write(in_9), .out_4(binary_cell_28_out_4));
  Binary_Cell binary_cell_29 (.Input(in_4), .Select(decoder_1_out_8), .Read_Write(in_9), .out_4(binary_cell_29_out_4));
  Binary_Cell binary_cell_30 (.Input(in_4), .Select(decoder_1_out_7), .Read_Write(in_9), .out_4(binary_cell_30_out_4));
  Binary_Cell binary_cell_31 (.Input(in_4), .Select(decoder_1_out_6), .Read_Write(in_9), .out_4(binary_cell_31_out_4));
  Binary_Cell binary_cell_32 (.Input(in_4), .Select(decoder_1_out_5), .Read_Write(in_9), .out_4(binary_cell_32_out_4));
  or or_4 (out_13, binary_cell_32_out_4, binary_cell_31_out_4, binary_cell_30_out_4, binary_cell_29_out_4, binary_cell_28_out_4, binary_cell_27_out_4, binary_cell_26_out_4, binary_cell_25_out_4);
endmodule
