// Logisim project 231488347_lab03_circuit.circ as structural Verilog: 3 circuits, main circuit main
module main (
  input  [2:0] DA,
  input  write,
  input  [3:0] D,
  input  [2:0] BA,
  input  [2:0] AA,
  output A3,
  output A2,
  output A1,
  output A0,
  output B3,
  output B2,
  output B1,
  output B0
);

  _4x8_Register_File u_4x8_register_file_1 (
    .WRITE(write), .DA(DA), .BA(BA), .AA(AA), .D(D), .A3(A3), .A2(A2), .A1(A1), .A0(A0), .B3(B3), .B2(B2),
    .B1(B1), .B0(B0));

  // Notes on the sheet:
  //   4X8 Register File
endmodule

module _4x8_Register_File (
  input  [3:0] D,
  input  WRITE,
  input  [2:0] DA,
  input  [2:0] BA,
  input  [2:0] AA,
  output A3,
  output A2,
  output A1,
  output A0,
  output B3,
  output B2,
  output B1,
  output B0
);

  wire clock_1_out, decoder_1_out0, decoder_1_out1, decoder_1_out2, decoder_1_out3, decoder_1_out4,
       decoder_1_out5, decoder_1_out6, decoder_1_out7;
  wire [3:0] R0_q, R1_q, R2_q, R3_q, R4_q, R5_q, R6_q, R7_q;

  Decoder #(.select(3)) decoder_1 (
    .out0(decoder_1_out0), .out1(decoder_1_out1), .out2(decoder_1_out2), .out3(decoder_1_out3),
    .out4(decoder_1_out4), .out5(decoder_1_out5), .out6(decoder_1_out6), .out7(decoder_1_out7), .sel(DA),
    .en(WRITE));
  Register #(.width(4)) R0 (.D(D), .en(decoder_1_out0), .Q(R0_q), .clk(clock_1_out));  // open: clr
  Register #(.width(4)) R2 (.D(D), .en(decoder_1_out2), .Q(R2_q), .clk(clock_1_out));  // open: clr
  Register #(.width(4)) R4 (.D(D), .en(decoder_1_out4), .Q(R4_q), .clk(clock_1_out));  // open: clr
  Register #(.width(4)) R6 (.D(D), .en(decoder_1_out6), .Q(R6_q), .clk(clock_1_out));  // open: clr
  Clock clock_1 (.out(clock_1_out));
  Register #(.width(4)) R1 (.D(D), .en(decoder_1_out1), .Q(R1_q), .clk(clock_1_out));  // open: clr
  Register #(.width(4)) R3 (.D(D), .en(decoder_1_out3), .Q(R3_q), .clk(clock_1_out));  // open: clr
  Register #(.width(4)) R5 (.D(D), .en(decoder_1_out5), .Q(R5_q), .clk(clock_1_out));  // open: clr
  Register #(.width(4)) R7 (.en(decoder_1_out7), .Q(R7_q), .clk(clock_1_out));  // open: D, clr
  Multiplexer #(.select(3)) multiplexer_1 (
    .in0(R0_q[3]), .in1(R1_q[3]), .in2(R2_q[3]), .in3(R3_q[3]), .in4(R4_q[3]), .in5(R5_q[3]), .in6(R6_q[3]),
    .in7(R7_q[3]), .out(A3), .sel(AA));  // open: en
  Multiplexer #(.select(3)) multiplexer_2 (
    .in0(R0_q[2]), .in1(R1_q[2]), .in2(R2_q[2]), .in3(R3_q[2]), .in4(R4_q[2]), .in5(R5_q[2]), .in6(R6_q[2]),
    .in7(R7_q[2]), .out(A2), .sel(AA));  // open: en
  Multiplexer #(.select(3)) multiplexer_3 (
    .in0(R0_q[1]), .in1(R1_q[1]), .in2(R2_q[1]), .in3(R3_q[1]), .in4(R4_q[1]), .in5(R5_q[1]), .in6(R6_q[1]),
    .in7(R7_q[1]), .out(A1), .sel(AA));  // open: en
  Multiplexer #(.select(3)) multiplexer_4 (
    .in0(R0_q[0]), .in1(R1_q[0]), .in2(R2_q[0]), .in3(R3_q[0]), .in4(R4_q[0]), .in5(R5_q[0]), .in6(R6_q[0]),
    .in7(R7_q[0]), .out(A0), .sel(AA));  // open: en
  Multiplexer #(.select(3)) multiplexer_5 (
    .in0(R0_q[3]), .in1(R1_q[3]), .in2(R2_q[3]), .in3(R3_q[3]), .in4(R4_q[3]), .in5(R5_q[3]), .in6(R6_q[3]),
    .in7(R7_q[3]), .out(B3), .sel(BA));  // open: en
  Multiplexer #(.select(3)) multiplexer_6 (
    .in0(R0_q[2]), .in1(R1_q[2]), .in2(R2_q[2]), .in3(R3_q[2]), .in4(R4_q[2]), .in5(R5_q[2]), .in6(R6_q[2]),
    .in7(R7_q[2]), .out(B2), .sel(BA));  // open: en
  Multiplexer #(.select(3)) multiplexer_7 (
    .in0(R0_q[1]), .in1(R1_q[1]), .in2(R2_q[1]), .in3(R3_q[1]), .in4(R4_q[1]), .in5(R5_q[1]), .in6(R6_q[1]),
    .in7(R7_q[1]), .out(B1), .sel(BA));  // open: en
  Multiplexer #(.select(3)) multiplexer_8 (
    .in0(R0_q[0]), .in1(R1_q[0]), .in2(R2_q[0]), .in3(R3_q[0]), .in4(R4_q[0]), .in5(R5_q[0]), .in6(R6_q[0]),
    .in7(R7_q[0]), .out(B0), .sel(BA));  // open: en
endmodule

module Extra (
  input  [1:0] in_1,
  input  [3:0] in_2,
  input  [1:0] in_3,
  input  [3:0] in_4,
  input  in_5,
  input  [1:0] in_6,
  output out_7,
  output out_8,
  output out_9,
  output out_10
);

  wire clock_1_out, decoder_1_out0, decoder_1_out1;
  wire [3:0] register_1_q, register_2_q;

  Decoder decoder_1 (.out0(decoder_1_out0), .out1(decoder_1_out1), .sel(in_5));  // open: en
  Clock clock_1 (.out(clock_1_out));
  Register #(.width(4)) register_1 (.D(in_2), .en(decoder_1_out0), .Q(register_1_q), .clk(clock_1_out));  // open: clr
  Register #(.width(4)) register_2 (.D(in_4), .en(decoder_1_out1), .Q(register_2_q), .clk(clock_1_out));  // open: clr
  Multiplexer #(.select(2)) multiplexer_1 (
    .in0(register_1_q[0]), .in1(register_1_q[1]), .in2(register_1_q[2]), .in3(register_1_q[3]), .out(out_9),
    .sel(in_3));  // open: en
  Multiplexer #(.select(2)) multiplexer_2 (
    .in0(register_2_q[0]), .in1(register_2_q[1]), .in2(register_2_q[2]), .in3(register_2_q[3]), .out(out_10),
    .sel(in_6));  // open: en

  assign out_7 = in_1[0];
  assign out_8 = in_1[1];
endmodule
