// Logisim project Data Path.circ as structural Verilog: 11 circuits, main circuit main
module main (
  input  [3:0] Data_Input,
  input  User_Input_Select,
  input  Register___Write,
  input  [1:0] DA,
  input  [3:0] FS___ALU_operators,
  input  [1:0] BA,
  input  [1:0] AA,
  input  RAM___Write_Read,
  input  ALU_RAM___select,
  output Cout,
  output G3,
  output G2,
  output G1,
  output G0
);

  DATA_PATH data_path_1 (
    .Register___Write(Register___Write), .DA(DA), .BA(BA), .AA(AA), .RAM___Write_Read(RAM___Write_Read),
    .ALU_RAM___select(ALU_RAM___select), .Uin3(Data_Input[3]), .Uin2(Data_Input[2]), .Uin1(Data_Input[1]),
    .Uin0(Data_Input[0]), .User_Input_Select(User_Input_Select), .G3(G3), .G2(G2), .G1(G1), .G0(G0),
    .Cout(Cout), .S3(FS___ALU_operators[3]), .S2(FS___ALU_operators[2]), .S1(FS___ALU_operators[1]),
    .S0(FS___ALU_operators[0]));

  // Notes on the sheet:
  //   Data
  //   Path
endmodule

module Sample_Work (
  input  in_1,
  input  in_2,
  input  in_3,
  input  Carry_in,
  input  Carry_in_2,
  input  in_6,
  input  in_7,
  input  in_8,
  input  in_9,
  input  Input1,
  input  Input1_2,
  input  in_12,
  input  Input2,
  input  Input2_2,
  input  [1:0] Select,
  input  in_16,
  input  [3:0] Input,
  input  [1:0] Select_2,
  input  Enable,
  input  Enable_2,
  input  Carry_in_3,
  input  Input1_3,
  input  Input2_3,
  input  [3:0] Input_2,
  input  Enable_3,
  input  Enable_4,
  input  [3:0] Input_3,
  input  [1:0] Select_3,
  input  [1:0] Select_4,
  input  [3:0] Input_4,
  input  S,
  input  R,
  input  Enable_5,
  input  Enable_6,
  input  [3:0] Data_Input,
  input  [3:0] Input_X,
  input  [3:0] Input_Y,
  input  Register___Write,
  input  Cin,
  input  [1:0] DA,
  input  [1:0] BA,
  input  [1:0] AA,
  input  [3:0] Input_5,
  input  [3:0] Input_6,
  input  [1:0] in_45,
  input  [3:0] Input_X_2,
  input  [3:0] Input_X_3,
  input  [3:0] Input_7,
  input  [3:0] Input_Y_2,
  input  [3:0] Input_Y_3,
  input  Select_5,
  input  in_52,
  input  [3:0] Address,
  input  [2:0] S_2,
  input  Write_Read,
  input  [3:0] Input_X_4,
  input  [3:0] Input_Y_4,
  input  Select_6,
  input  Data_Input_2,
  input  S3,
  input  S2,
  input  S1,
  input  S0,
  input  Write_Read_2,
  output out_65,
  output out_66,
  output out_67,
  output out_68,
  output Carry_out,
  output Carry_out_2,
  output out_71,
  output [3:0] Output,
  output out_73,
  output out_74,
  output out_75,
  output out_76,
  output out_77,
  output out_78,
  output out_79,
  output out_80,
  output Carry_out_3,
  output out_82,
  output out_83,
  output out_84,
  output out_85,
  output out_86,
  output out_87,
  output out_88,
  output out_89,
  output out_90,
  output [3:0] Output_2,
  output Q,
  output Q_prime,
  output [3:0] Output_3,
  output [3:0] Output_4,
  output Cout,
  output [3:0] Output_5,
  output [3:0] Output_6,
  output [3:0] Output_7,
  output Cout_2,
  output [3:0] Output_8,
  output [3:0] Output_9,
  output Cout_3,
  output Output_10,
  output [3:0] Output_11
);

  wire Clock_2_out, Clock_out;

  Register #(.width(4)) register_1 (.D(Input_4), .en(Enable_5), .Q(Output_2), .clk(Clock_out));  // open: clr
  Clock Clock (.out(Clock_out));
  Adder #(.width(1)) adder_1 (.a(Input1), .b(Input2), .out(out_67), .cin(Carry_in), .cout(Carry_out));
  Adder #(.width(1)) adder_2 (.a(Input1_3), .b(Input2_3), .out(out_75), .cin(Carry_in_3), .cout(Carry_out_3));
  Arithmetic_unit___ALU_subcircuit arithmetic_unit_alu_subcircuit_1 (
    .Y3(Input_Y_2[3]), .Y2(Input_Y_2[2]), .Y1(Input_Y_2[1]), .Y0(Input_Y_2[0]), .X3(Input_X_2[3]),
    .X2(Input_X_2[2]), .X1(Input_X_2[1]), .X0(Input_X_2[0]), .S2(S_2[2]), .S1(S_2[1]), .S0(S_2[0]),
    .G3(Output_8[3]), .G2(Output_8[2]), .G1(Output_8[1]), .G0(Output_8[0]), .Cout(Cout_2));
  _4x4_register_File u_4x4_register_file_1 (
    .WRITE(Register___Write), .DA(DA), .AA(AA), .D3(Data_Input[3]), .D2(Data_Input[2]), .D1(Data_Input[1]),
    .D0(Data_Input[0]), .A3(Output_5[3]), .A2(Output_5[2]), .A1(Output_5[1]), .A0(Output_5[0]),
    .B3(Output_6[3]), .B2(Output_6[2]), .B1(Output_6[1]), .B0(Output_6[0]), .BA(BA));
  Clock Clock_2 (.out(Clock_2_out));
  Adder #(.width(1)) adder_3 (.a(Input1_2), .b(Input2_2), .out(out_68), .cin(Carry_in_2), .cout(Carry_out_2));
  S_R_Flip_Flop s_r_ff_1 (.S(S), .clk(Clock_2_out), .R(R), .Q(Q), .Qn(Q_prime), .en(Enable_6));  // open: preset, reset
  _4bit_adder___Arithmetic_unit_Subcircuit u_4bit_adder_arithmetic_unit_subcircuit_1 (
    .Cin(Cin), .A0(Input_5[0]), .A1(Input_5[1]), .A2(Input_5[2]), .A3(Input_5[3]), .B0(Input_6[0]),
    .B1(Input_6[1]), .B2(Input_6[2]), .B3(Input_6[3]), .S0(Output_3[0]), .S1(Output_3[1]), .S2(Output_3[2]),
    .S3(Output_3[3]), .cout(Cout));
  ALU alu_1 (
    .X3(Input_X_4[3]), .X2(Input_X_4[2]), .X1(Input_X_4[1]), .X0(Input_X_4[0]), .Y3(Input_Y_4[3]),
    .Y2(Input_Y_4[2]), .Y1(Input_Y_4[1]), .Y0(Input_Y_4[0]), .S3(S3), .S2(S2), .S1(S1), .S0(S0),
    .Cout(Cout_3), .G3(Output_11[3]), .G2(Output_11[2]), .G1(Output_11[1]), .G0(Output_11[0]));
  Decoder #(.select(2)) decoder_1 (
    .out0(out_79), .out1(out_82), .out2(out_85), .out3(out_88), .sel(Select_4), .en(Enable_4));
  Multiplexer #(.select(2)) multiplexer_1 (
    .in0(in_2), .in1(in_6), .in2(in_8), .in3(in_12), .out(out_66), .sel(Select_2), .en(Enable_2));
  Quad_2x1_Set_of_Mux quad_2x1_set_of_mux_1 (
    .A3(Input_X_3[3]), .A2(Input_X_3[2]), .A1(Input_X_3[1]), .A0(Input_X_3[0]), .L3(Input_Y_3[3]),
    .L2(Input_Y_3[2]), .L1(Input_Y_3[1]), .L0(Input_Y_3[0]), .S(in_52), ._03(Output_7[3]), ._02(Output_7[2]),
    ._01(Output_7[1]), .O0(Output_7[0]));
  Decoder #(.select(2)) decoder_2 (
    .out0(out_78), .out1(out_80), .out2(out_83), .out3(out_86), .sel(Select_3), .en(Enable_3));
  Binary_cell___RAM_subcircuit binary_cell_ram_subcircuit_1 (
    .Input(Data_Input_2), .Select(Select_6), .Read_Write(Write_Read_2), .Output(Output_10));
  Multiplexer #(.select(2)) multiplexer_2 (
    .in0(in_1), .in1(in_3), .in2(in_7), .in3(in_9), .out(out_65), .sel(Select), .en(Enable));
  Logic_Unit___ALU_subcircuit logic_unit_alu_subcircuit_1 (
    .X3(Input_X[3]), .X2(Input_X[2]), .X1(Input_X[1]), .X0(Input_X[0]), .Y3(Input_Y[3]), .Y2(Input_Y[2]),
    .Y1(Input_Y[1]), .Y0(Input_Y[0]), .S0(in_45[0]), .S1(in_45[1]), .G3(Output_4[3]), .G2(Output_4[2]),
    .G1(Output_4[1]), .G0(Output_4[0]));
  _16x4_RAM u_16x4_ram_1 (
    .RAM_select(Select_5), .Address(Address), .Read_Write(Write_Read), .I3(Input_7[3]), .I2(Input_7[2]),
    .I1(Input_7[1]), .I0(Input_7[0]), .O3(Output_9[3]), .O2(Output_9[2]), .O1(Output_9[1]), .O0(Output_9[0]));

  assign out_73 = Input_2[0];
  assign out_74 = Input_2[1];
  assign out_76 = Input_2[2];
  assign out_77 = Input_2[3];
  assign out_84 = Input_3[0];
  assign out_87 = Input_3[1];
  assign out_89 = Input_3[2];
  assign out_90 = Input_3[3];

  // Notes on the sheet:
  //   1
  //   2
  //   4x4
  //   Register File
  //   Arithmetic Unit
  //   3
  //   ALU
  //   LogicUnit
  //   16x4
  //   RAM
endmodule

module _4bit_adder___Arithmetic_unit_Subcircuit (
  input  Cin,
  input  A0,
  input  A1,
  input  A2,
  input  A3,
  input  B0,
  input  B1,
  input  B2,
  input  B3,
  output S0,
  output S1,
  output S2,
  output S3,
  output cout
);

  wire adder_1_cout, adder_2_cout, adder_3_cout;

  Adder #(.width(1)) adder_1 (.a(B0), .b(A0), .out(S0), .cin(Cin), .cout(adder_1_cout));
  Adder #(.width(1)) adder_2 (.a(B1), .b(A1), .out(S1), .cin(adder_1_cout), .cout(adder_2_cout));
  Adder #(.width(1)) adder_3 (.a(B2), .b(A2), .out(S2), .cin(adder_2_cout), .cout(adder_3_cout));
  Adder #(.width(1)) adder_4 (.a(B3), .b(A3), .out(S3), .cin(adder_3_cout), .cout(cout));
endmodule

module Arithmetic_unit___ALU_subcircuit (
  input  X3,
  input  X2,
  input  X1,
  input  X0,
  input  Y3,
  input  Y2,
  input  Y1,
  input  Y0,
  input  S2,
  input  S1,
  input  S0,
  output G3,
  output G2,
  output G1,
  output G0,
  output Cout
);

  wire and_1_out, and_2_out, and_3_out, and_4_out, and_5_out, and_6_out, and_7_out, and_8_out, not_1_out,
       not_2_out, not_3_out, not_4_out, or_1_out, or_2_out, or_3_out, or_4_out;

  not not_1 (not_1_out, Y3);
  not not_2 (not_2_out, Y2);
  not not_3 (not_3_out, Y1);
  not not_4 (not_4_out, Y0);
  and and_1 (and_1_out, not_1_out, S2);
  and and_2 (and_2_out, Y3, S1);
  and and_3 (and_3_out, not_2_out, S2);
  and and_4 (and_4_out, Y2, S1);
  and and_5 (and_5_out, not_3_out, S2);
  and and_6 (and_6_out, Y1, S1);
  and and_7 (and_7_out, not_4_out, S2);
  and and_8 (and_8_out, Y0, S1);
  or or_1 (or_1_out, and_1_out, and_2_out);
  or or_2 (or_2_out, and_3_out, and_4_out);
  or or_3 (or_3_out, and_5_out, and_6_out);
  or or_4 (or_4_out, and_7_out, and_8_out);
  _4bit_adder___Arithmetic_unit_Subcircuit u_4bit_adder_arithmetic_unit_subcircuit_1 (
    .Cin(S0), .A0(or_4_out), .A1(or_3_out), .A2(or_2_out), .A3(or_1_out), .B0(X0), .B1(X1), .B2(X2), .B3(X3),
    .S0(G0), .S1(G1), .S2(G2), .S3(G3), .cout(Cout));

  // Notes on the sheet:
  //   4-Bit
  //   Adder
endmodule

module Logic_Unit___ALU_subcircuit (
  input  X3,
  input  Y3,
  input  X2,
  input  Y2,
  input  X1,
  input  Y1,
  input  X0,
  input  Y0,
  input  S0,
  input  S1,
  output G3,
  output G2,
  output G1,
  output G0
);

  wire and_1_out, and_2_out, and_3_out, and_4_out, not_1_out, not_2_out, not_3_out, not_4_out, or_1_out,
       or_2_out, or_3_out, or_4_out, xor_1_out, xor_2_out, xor_3_out, xor_4_out;

  and and_1 (and_1_out, X3, Y3);
  or or_1 (or_1_out, X3, Y3);
  not not_1 (not_1_out, X3);
  and and_2 (and_2_out, X2, Y2);
  or or_2 (or_2_out, X2, Y2);
  not not_2 (not_2_out, X2);
  and and_3 (and_3_out, X1, Y1);
  or or_3 (or_3_out, X1, Y1);
  not not_3 (not_3_out, X1);
  and and_4 (and_4_out, X0, Y0);
  or or_4 (or_4_out, X0, Y0);
  not not_4 (not_4_out, X0);
  xor xor_1 (xor_1_out, X3, Y3);
  xor xor_2 (xor_2_out, X2, Y2);
  xor xor_3 (xor_3_out, X1, Y1);
  xor xor_4 (xor_4_out, X0, Y0);
  Multiplexer #(.select(2)) multiplexer_1 (
    .in0(and_1_out), .in1(xor_1_out), .in2(or_1_out), .in3(not_1_out), .out(G3), .sel({S1, S0}));  // open: en
  Multiplexer #(.select(2)) multiplexer_2 (
    .in0(and_2_out), .in1(xor_2_out), .in2(or_2_out), .in3(not_2_out), .out(G2), .sel({S1, S0}));  // open: en
  Multiplexer #(.select(2)) multiplexer_3 (
    .in0(and_3_out), .in1(xor_3_out), .in2(or_3_out), .in3(not_3_out), .out(G1), .sel({S1, S0}));  // open: en
  Multiplexer #(.select(2)) multiplexer_4 (
    .in0(and_4_out), .in1(xor_4_out), .in2(or_4_out), .in3(not_4_out), .out(G0), .sel({S1, S0}));  // open: en
endmodule

// Binary Cell
module Binary_cell___RAM_subcircuit (
  input  Select,
  input  Input,
  input  Read_Write,
  output Output
);

  wire and_1_out, and_2_out, clock_1_out, not_1_out, not_2_out, s_r_ff_1_q;

  not not_1 (not_1_out, Input);
  and and_1 (and_1_out, Select, not_1_out, not_2_out);
  and and_2 (and_2_out, Select, Input, not_2_out);
  Clock clock_1 (.out(clock_1_out));
  not not_2 (not_2_out, Read_Write);
  S_R_Flip_Flop s_r_ff_1 (
    .S(and_2_out), .clk(clock_1_out), .R(and_1_out), .Q(s_r_ff_1_q));  // open: Qn, preset, reset, en
  and and_3 (Output, Select, s_r_ff_1_q, Read_Write);
endmodule

module Quad_2x1_Set_of_Mux (
  input  A3,
  input  A2,
  input  A1,
  input  A0,
  input  L3,
  input  L2,
  input  L1,
  input  L0,
  input  S,
  output _03,
  output _02,
  output _01,
  output O0
);

  wire undriven;

  Multiplexer multiplexer_1 (.in0(A0), .in1(L0), .out(O0), .sel(S));  // open: en
  Multiplexer multiplexer_2 (.in0(A3), .in1(L3), .out(_03), .sel(S), .en(undriven));
  Multiplexer multiplexer_3 (.in0(A2), .in1(L2), .out(_02), .sel(S));  // open: en
  Multiplexer multiplexer_4 (.in0(A1), .in1(L1), .out(_01), .sel(S));  // open: en
endmodule

module ALU (
  input  X3,
  input  X2,
  input  X1,
  input  X0,
  input  Y3,
  input  Y2,
  input  Y1,
  input  Y0,
  input  S3,
  input  S2,
  input  S1,
  input  S0,
  output Cout,
  output G3,
  output G2,
  output G1,
  output G0
);

  wire arithmetic_unit_alu_subcircuit_1_g0, arithmetic_unit_alu_subcircuit_1_g1,
       arithmetic_unit_alu_subcircuit_1_g2, arithmetic_unit_alu_subcircuit_1_g3,
       logic_unit_alu_subcircuit_1_g0, logic_unit_alu_subcircuit_1_g1, logic_unit_alu_subcircuit_1_g2,
       logic_unit_alu_subcircuit_1_g3;

  Arithmetic_unit___ALU_subcircuit arithmetic_unit_alu_subcircuit_1 (
    .Y3(Y3), .Y2(Y2), .Y1(Y1), .Y0(Y0), .X3(X3), .X2(X2), .X1(X1), .X0(X0), .S2(S2), .S1(S1), .S0(S0),
    .G3(arithmetic_unit_alu_subcircuit_1_g3), .G2(arithmetic_unit_alu_subcircuit_1_g2),
    .G1(arithmetic_unit_alu_subcircuit_1_g1), .G0(arithmetic_unit_alu_subcircuit_1_g0), .Cout(Cout));
  Logic_Unit___ALU_subcircuit logic_unit_alu_subcircuit_1 (
    .X3(X3), .X2(X2), .X1(X1), .X0(X0), .Y3(Y3), .Y2(Y2), .Y1(Y1), .Y0(Y0), .S0(S0), .S1(S1),
    .G3(logic_unit_alu_subcircuit_1_g3), .G2(logic_unit_alu_subcircuit_1_g2),
    .G1(logic_unit_alu_subcircuit_1_g1), .G0(logic_unit_alu_subcircuit_1_g0));
  Quad_2x1_Set_of_Mux quad_2x1_set_of_mux_1 (
    .A3(arithmetic_unit_alu_subcircuit_1_g3), .A2(arithmetic_unit_alu_subcircuit_1_g2),
    .A1(arithmetic_unit_alu_subcircuit_1_g1), .A0(arithmetic_unit_alu_subcircuit_1_g0),
    .L3(logic_unit_alu_subcircuit_1_g3), .L2(logic_unit_alu_subcircuit_1_g2),
    .L1(logic_unit_alu_subcircuit_1_g1), .L0(logic_unit_alu_subcircuit_1_g0), .S(S3), ._03(G3), ._02(G2),
    ._01(G1), .O0(G0));

  // Notes on the sheet:
  //   Y
  //   X
  //   X
  //   Arithmetic Unit
  //   Y
  //   LogicUnit
  //   2x1
  //   Control
  //   MUX
endmodule

module _4x4_register_File (
  input  D3,
  input  D2,
  input  D1,
  input  D0,
  input  WRITE,
  input  [1:0] DA,
  input  [1:0] AA,
  input  [1:0] BA,
  output A3,
  output A2,
  output A1,
  output A0,
  output B3,
  output B2,
  output B1,
  output B0
);

  wire clock_1_out, decoder_1_out0, decoder_1_out1, decoder_1_out2, decoder_1_out3;
  wire [3:0] R0_q, R1_q, R2_q, R3_q;

  Decoder #(.select(2)) decoder_1 (
    .out0(decoder_1_out0), .out1(decoder_1_out1), .out2(decoder_1_out2), .out3(decoder_1_out3), .sel(DA),
    .en(WRITE));
  Register #(.width(4)) R0 (.D({D3, D2, D1, D0}), .en(decoder_1_out0), .Q(R0_q), .clk(clock_1_out));  // open: clr
  Register #(.width(4)) R2 (.D({D3, D2, D1, D0}), .en(decoder_1_out2), .Q(R2_q), .clk(clock_1_out));  // open: clr
  Clock clock_1 (.out(clock_1_out));
  Register #(.width(4)) R1 (.D({D3, D2, D1, D0}), .en(decoder_1_out1), .Q(R1_q), .clk(clock_1_out));  // open: clr
  Register #(.width(4)) R3 (.D({D3, D2, D1, D0}), .en(decoder_1_out3), .Q(R3_q), .clk(clock_1_out));  // open: clr
  Multiplexer #(.select(2)) multiplexer_1 (
    .in0(R0_q[3]), .in1(R1_q[3]), .in2(R2_q[3]), .in3(R3_q[3]), .out(A3), .sel(AA));  // open: en
  Multiplexer #(.select(2)) multiplexer_2 (
    .in0(R0_q[2]), .in1(R1_q[2]), .in2(R2_q[2]), .in3(R3_q[2]), .out(A2), .sel(AA));  // open: en
  Multiplexer #(.select(2)) multiplexer_3 (
    .in0(R0_q[1]), .in1(R1_q[1]), .in2(R2_q[1]), .in3(R3_q[1]), .out(A1), .sel(AA));  // open: en
  Multiplexer #(.select(2)) multiplexer_4 (
    .in0(R0_q[0]), .in1(R1_q[0]), .in2(R2_q[0]), .in3(R3_q[0]), .out(A0), .sel(AA));  // open: en
  Multiplexer #(.select(2)) multiplexer_5 (
    .in0(R0_q[3]), .in1(R1_q[3]), .in2(R2_q[3]), .in3(R3_q[3]), .out(B3), .sel(BA));  // open: en
  Multiplexer #(.select(2)) multiplexer_6 (
    .in0(R0_q[2]), .in1(R1_q[2]), .in2(R2_q[2]), .in3(R3_q[2]), .out(B2), .sel(BA));  // open: en
  Multiplexer #(.select(2)) multiplexer_7 (
    .in0(R0_q[1]), .in1(R1_q[1]), .in2(R2_q[1]), .in3(R3_q[1]), .out(B1), .sel(BA));  // open: en
  Multiplexer #(.select(2)) multiplexer_8 (
    .in0(R0_q[0]), .in1(R1_q[0]), .in2(R2_q[0]), .in3(R3_q[0]), .out(B0), .sel(BA));  // open: en
endmodule

module _16x4_RAM (
  input  I3,
  input  I2,
  input  I1,
  input  I0,
  input  RAM_select,
  input  [3:0] Address,
  input  Read_Write,
  output O3,
  output O2,
  output O1,
  output O0
);

  wire binary_cell_ram_subcircuit_1_output, binary_cell_ram_subcircuit_2_output,
       binary_cell_ram_subcircuit_3_output, binary_cell_ram_subcircuit_4_output,
       binary_cell_ram_subcircuit_5_output, binary_cell_ram_subcircuit_6_output,
       binary_cell_ram_subcircuit_7_output, binary_cell_ram_subcircuit_8_output,
       binary_cell_ram_subcircuit_9_output, binary_cell_ram_subcircuit_10_output,
       binary_cell_ram_subcircuit_11_output, binary_cell_ram_subcircuit_12_output,
       binary_cell_ram_subcircuit_13_output, binary_cell_ram_subcircuit_14_output,
       binary_cell_ram_subcircuit_15_output, binary_cell_ram_subcircuit_16_output,
       binary_cell_ram_subcircuit_17_output, binary_cell_ram_subcircuit_18_output,
       binary_cell_ram_subcircuit_19_output, binary_cell_ram_subcircuit_20_output,
       binary_cell_ram_subcircuit_21_output, binary_cell_ram_subcircuit_22_output,
       binary_cell_ram_subcircuit_23_output, binary_cell_ram_subcircuit_24_output,
       binary_cell_ram_subcircuit_25_output, binary_cell_ram_subcircuit_26_output,
       binary_cell_ram_subcircuit_27_output, binary_cell_ram_subcircuit_28_output,
       binary_cell_ram_subcircuit_29_output, binary_cell_ram_subcircuit_30_output,
       binary_cell_ram_subcircuit_31_output, binary_cell_ram_subcircuit_32_output,
       binary_cell_ram_subcircuit_33_output, binary_cell_ram_subcircuit_34_output,
       binary_cell_ram_subcircuit_35_output, binary_cell_ram_subcircuit_36_output,
       binary_cell_ram_subcircuit_37_output, binary_cell_ram_subcircuit_38_output,
       binary_cell_ram_subcircuit_39_output, binary_cell_ram_subcircuit_40_output,
       binary_cell_ram_subcircuit_41_output, binary_cell_ram_subcircuit_42_output,
       binary_cell_ram_subcircuit_43_output, binary_cell_ram_subcircuit_44_output,
       binary_cell_ram_subcircuit_45_output, binary_cell_ram_subcircuit_46_output,
       binary_cell_ram_subcircuit_47_output, binary_cell_ram_subcircuit_48_output,
       binary_cell_ram_subcircuit_49_output, binary_cell_ram_subcircuit_50_output,
       binary_cell_ram_subcircuit_51_output, binary_cell_ram_subcircuit_52_output,
       binary_cell_ram_subcircuit_53_output, binary_cell_ram_subcircuit_54_output,
       binary_cell_ram_subcircuit_55_output, binary_cell_ram_subcircuit_56_output,
       binary_cell_ram_subcircuit_57_output, binary_cell_ram_subcircuit_58_output,
       binary_cell_ram_subcircuit_59_output, binary_cell_ram_subcircuit_60_output,
       binary_cell_ram_subcircuit_61_output, binary_cell_ram_subcircuit_62_output,
       binary_cell_ram_subcircuit_63_output, binary_cell_ram_subcircuit_64_output, decoder_1_out0,
       decoder_1_out1, decoder_1_out2, decoder_1_out3, decoder_1_out4, decoder_1_out5, decoder_1_out6,
       decoder_1_out7, decoder_1_out8, decoder_1_out9, decoder_1_out10, decoder_1_out11, decoder_1_out12,
       decoder_1_out13, decoder_1_out14, decoder_1_out15;

  Decoder #(.select(4)) decoder_1 (
    .out0(decoder_1_out0), .out1(decoder_1_out1), .out2(decoder_1_out2), .out3(decoder_1_out3),
    .out4(decoder_1_out4), .out5(decoder_1_out5), .out6(decoder_1_out6), .out7(decoder_1_out7),
    .out8(decoder_1_out8), .out9(decoder_1_out9), .out10(decoder_1_out10), .out11(decoder_1_out11),
    .out12(decoder_1_out12), .out13(decoder_1_out13), .out14(decoder_1_out14), .out15(decoder_1_out15),
    .sel(Address), .en(RAM_select));
  Binary_cell___RAM_subcircuit binary_cell_ram_subcircuit_1 (
    .Input(I3), .Select(decoder_1_out0), .Read_Write(Read_Write), .Output(binary_cell_ram_subcircuit_1_output));
  Binary_cell___RAM_subcircuit binary_cell_ram_subcircuit_2 (
    .Input(I3), .Select(decoder_1_out1), .Read_Write(Read_Write), .Output(binary_cell_ram_subcircuit_2_output));
  Binary_cell___RAM_subcircuit binary_cell_ram_subcircuit_3 (
    .Input(I3), .Select(decoder_1_out2), .Read_Write(Read_Write), .Output(binary_cell_ram_subcircuit_3_output));
  Binary_cell___RAM_subcircuit binary_cell_ram_subcircuit_4 (
    .Input(I3), .Select(decoder_1_out3), .Read_Write(Read_Write), .Output(binary_cell_ram_subcircuit_4_output));
  Binary_cell___RAM_subcircuit binary_cell_ram_subcircuit_5 (
    .Input(I3), .Select(decoder_1_out4), .Read_Write(Read_Write), .Output(binary_cell_ram_subcircuit_5_output));
  Binary_cell___RAM_subcircuit binary_cell_ram_subcircuit_6 (
    .Input(I3), .Select(decoder_1_out5), .Read_Write(Read_Write), .Output(binary_cell_ram_subcircuit_6_output));
  Binary_cell___RAM_subcircuit binary_cell_ram_subcircuit_7 (
    .Input(I3), .Select(decoder_1_out6), .Read_Write(Read_Write), .Output(binary_cell_ram_subcircuit_7_output));
  Binary_cell___RAM_subcircuit binary_cell_ram_subcircuit_8 (
    .Input(I3), .Select(decoder_1_out7), .Read_Write(Read_Write), .Output(binary_cell_ram_subcircuit_8_output));
  Binary_cell___RAM_subcircuit binary_cell_ram_subcircuit_9 (
    .Input(I3), .Select(decoder_1_out8), .Read_Write(Read_Write), .Output(binary_cell_ram_subcircuit_9_output));
  Binary_cell___RAM_subcircuit binary_cell_ram_subcircuit_10 (
    .Input(I3), .Select(decoder_1_out9), .Read_Write(Read_Write),
    .Output(binary_cell_ram_subcircuit_10_output));
  Binary_cell___RAM_subcircuit binary_cell_ram_subcircuit_11 (
    .Input(I3), .Select(decoder_1_out10), .Read_Write(Read_Write),
    .Output(binary_cell_ram_subcircuit_11_output));
  Binary_cell___RAM_subcircuit binary_cell_ram_subcircuit_12 (
    .Input(I3), .Select(decoder_1_out11), .Read_Write(Read_Write),
    .Output(binary_cell_ram_subcircuit_12_output));
  Binary_cell___RAM_subcircuit binary_cell_ram_subcircuit_13 (
    .Input(I3), .Select(decoder_1_out12), .Read_Write(Read_Write),
    .Output(binary_cell_ram_subcircuit_13_output));
  Binary_cell___RAM_subcircuit binary_cell_ram_subcircuit_14 (
    .Input(I3), .Select(decoder_1_out13), .Read_Write(Read_Write),
    .Output(binary_cell_ram_subcircuit_14_output));
  Binary_cell___RAM_subcircuit binary_cell_ram_subcircuit_15 (
    .Input(I3), .Select(decoder_1_out14), .Read_Write(Read_Write),
    .Output(binary_cell_ram_subcircuit_15_output));
  Binary_cell___RAM_subcircuit binary_cell_ram_subcircuit_16 (
    .Input(I3), .Select(decoder_1_out15), .Read_Write(Read_Write),
    .Output(binary_cell_ram_subcircuit_16_output));
  or or_1 (O3, binary_cell_ram_subcircuit_16_output, binary_cell_ram_subcircuit_15_output, binary_cell_ram_subcircuit_14_output, binary_cell_ram_subcircuit_13_output, binary_cell_ram_subcircuit_12_output, binary_cell_ram_subcircuit_11_output, binary_cell_ram_subcircuit_10_output, binary_cell_ram_subcircuit_9_output, binary_cell_ram_subcircuit_8_output, binary_cell_ram_subcircuit_7_output, binary_cell_ram_subcircuit_6_output, binary_cell_ram_subcircuit_5_output, binary_cell_ram_subcircuit_4_output, binary_cell_ram_subcircuit_3_output, binary_cell_ram_subcircuit_2_output, binary_cell_ram_subcircuit_1_output);
  Binary_cell___RAM_subcircuit binary_cell_ram_subcircuit_17 (
    .Input(I2), .Select(decoder_1_out0), .Read_Write(Read_Write),
    .Output(binary_cell_ram_subcircuit_17_output));
  Binary_cell___RAM_subcircuit binary_cell_ram_subcircuit_18 (
    .Input(I2), .Select(decoder_1_out1), .Read_Write(Read_Write),
    .Output(binary_cell_ram_subcircuit_18_output));
  Binary_cell___RAM_subcircuit binary_cell_ram_subcircuit_19 (
    .Input(I2), .Select(decoder_1_out2), .Read_Write(Read_Write),
    .Output(binary_cell_ram_subcircuit_19_output));
  Binary_cell___RAM_subcircuit binary_cell_ram_subcircuit_20 (
    .Input(I2), .Select(decoder_1_out3), .Read_Write(Read_Write),
    .Output(binary_cell_ram_subcircuit_20_output));
  Binary_cell___RAM_subcircuit binary_cell_ram_subcircuit_21 (
    .Input(I2), .Select(decoder_1_out4), .Read_Write(Read_Write),
    .Output(binary_cell_ram_subcircuit_21_output));
  Binary_cell___RAM_subcircuit binary_cell_ram_subcircuit_22 (
    .Input(I2), .Select(decoder_1_out5), .Read_Write(Read_Write),
    .Output(binary_cell_ram_subcircuit_22_output));
  Binary_cell___RAM_subcircuit binary_cell_ram_subcircuit_23 (
    .Input(I2), .Select(decoder_1_out6), .Read_Write(Read_Write),
    .Output(binary_cell_ram_subcircuit_23_output));
  Binary_cell___RAM_subcircuit binary_cell_ram_subcircuit_24 (
    .Input(I2), .Select(decoder_1_out7), .Read_Write(Read_Write),
    .Output(binary_cell_ram_subcircuit_24_output));
  Binary_cell___RAM_subcircuit binary_cell_ram_subcircuit_25 (
    .Input(I2), .Select(decoder_1_out8), .Read_Write(Read_Write),
    .Output(binary_cell_ram_subcircuit_25_output));
  Binary_cell___RAM_subcircuit binary_cell_ram_subcircuit_26 (
    .Input(I2), .Select(decoder_1_out9), .Read_Write(Read_Write),
    .Output(binary_cell_ram_subcircuit_26_output));
  Binary_cell___RAM_subcircuit binary_cell_ram_subcircuit_27 (
    .Input(I2), .Select(decoder_1_out10), .Read_Write(Read_Write),
    .Output(binary_cell_ram_subcircuit_27_output));
  Binary_cell___RAM_subcircuit binary_cell_ram_subcircuit_28 (
    .Input(I2), .Select(decoder_1_out11), .Read_Write(Read_Write),
    .Output(binary_cell_ram_subcircuit_28_output));
  Binary_cell___RAM_subcircuit binary_cell_ram_subcircuit_29 (
    .Input(I2), .Select(decoder_1_out12), .Read_Write(Read_Write),
    .Output(binary_cell_ram_subcircuit_29_output));
  Binary_cell___RAM_subcircuit binary_cell_ram_subcircuit_30 (
    .Input(I2), .Select(decoder_1_out13), .Read_Write(Read_Write),
    .Output(binary_cell_ram_subcircuit_30_output));
  Binary_cell___RAM_subcircuit binary_cell_ram_subcircuit_31 (
    .Input(I2), .Select(decoder_1_out14), .Read_Write(Read_Write),
    .Output(binary_cell_ram_subcircuit_31_output));
  Binary_cell___RAM_subcircuit binary_cell_ram_subcircuit_32 (
    .Input(I2), .Select(decoder_1_out15), .Read_Write(Read_Write),
    .Output(binary_cell_ram_subcircuit_32_output));
  or or_2 (O2, binary_cell_ram_subcircuit_32_output, binary_cell_ram_subcircuit_31_output, binary_cell_ram_subcircuit_30_output, binary_cell_ram_subcircuit_29_output, binary_cell_ram_subcircuit_28_output, binary_cell_ram_subcircuit_27_output, binary_cell_ram_subcircuit_26_output, binary_cell_ram_subcircuit_25_output, binary_cell_ram_subcircuit_24_output, binary_cell_ram_subcircuit_23_output, binary_cell_ram_subcircuit_22_output, binary_cell_ram_subcircuit_21_output, binary_cell_ram_subcircuit_20_output, binary_cell_ram_subcircuit_19_output, binary_cell_ram_subcircuit_18_output, binary_cell_ram_subcircuit_17_output);
  Binary_cell___RAM_subcircuit binary_cell_ram_subcircuit_33 (
    .Input(I1), .Select(decoder_1_out0), .Read_Write(Read_Write),
    .Output(binary_cell_ram_subcircuit_33_output));
  Binary_cell___RAM_subcircuit binary_cell_ram_subcircuit_34 (
    .Input(I1), .Select(decoder_1_out1), .Read_Write(Read_Write),
    .Output(binary_cell_ram_subcircuit_34_output));
  Binary_cell___RAM_subcircuit binary_cell_ram_subcircuit_35 (
    .Input(I1), .Select(decoder_1_out2), .Read_Write(Read_Write),
    .Output(binary_cell_ram_subcircuit_35_output));
  Binary_cell___RAM_subcircuit binary_cell_ram_subcircuit_36 (
    .Input(I1), .Select(decoder_1_out3), .Read_Write(Read_Write),
    .Output(binary_cell_ram_subcircuit_36_output));
  Binary_cell___RAM_subcircuit binary_cell_ram_subcircuit_37 (
    .Input(I1), .Select(decoder_1_out4), .Read_Write(Read_Write),
    .Output(binary_cell_ram_subcircuit_37_output));
  Binary_cell___RAM_subcircuit binary_cell_ram_subcircuit_38 (
    .Input(I1), .Select(decoder_1_out5), .Read_Write(Read_Write),
    .Output(binary_cell_ram_subcircuit_38_output));
  Binary_cell___RAM_subcircuit binary_cell_ram_subcircuit_39 (
    .Input(I1), .Select(decoder_1_out6), .Read_Write(Read_Write),
    .Output(binary_cell_ram_subcircuit_39_output));
  Binary_cell___RAM_subcircuit binary_cell_ram_subcircuit_40 (
    .Input(I1), .Select(decoder_1_out7), .Read_Write(Read_Write),
    .Output(binary_cell_ram_subcircuit_40_output));
  Binary_cell___RAM_subcircuit binary_cell_ram_subcircuit_41 (
    .Input(I1), .Select(decoder_1_out8), .Read_Write(Read_Write),
    .Output(binary_cell_ram_subcircuit_41_output));
  Binary_cell___RAM_subcircuit binary_cell_ram_subcircuit_42 (
    .Input(I1), .Select(decoder_1_out9), .Read_Write(Read_Write),
    .Output(binary_cell_ram_subcircuit_42_output));
  Binary_cell___RAM_subcircuit binary_cell_ram_subcircuit_43 (
    .Input(I1), .Select(decoder_1_out10), .Read_Write(Read_Write),
    .Output(binary_cell_ram_subcircuit_43_output));
  Binary_cell___RAM_subcircuit binary_cell_ram_subcircuit_44 (
    .Input(I1), .Select(decoder_1_out11), .Read_Write(Read_Write),
    .Output(binary_cell_ram_subcircuit_44_output));
  Binary_cell___RAM_subcircuit binary_cell_ram_subcircuit_45 (
    .Input(I1), .Select(decoder_1_out12), .Read_Write(Read_Write),
    .Output(binary_cell_ram_subcircuit_45_output));
  Binary_cell___RAM_subcircuit binary_cell_ram_subcircuit_46 (
    .Input(I1), .Select(decoder_1_out13), .Read_Write(Read_Write),
    .Output(binary_cell_ram_subcircuit_46_output));
  Binary_cell___RAM_subcircuit binary_cell_ram_subcircuit_47 (
    .Input(I1), .Select(decoder_1_out14), .Read_Write(Read_Write),
    .Output(binary_cell_ram_subcircuit_47_output));
  Binary_cell___RAM_subcircuit binary_cell_ram_subcircuit_48 (
    .Input(I1), .Select(decoder_1_out15), .Read_Write(Read_Write),
    .Output(binary_cell_ram_subcircuit_48_output));
  or or_3 (O1, binary_cell_ram_subcircuit_48_output, binary_cell_ram_subcircuit_47_output, binary_cell_ram_subcircuit_46_output, binary_cell_ram_subcircuit_45_output, binary_cell_ram_subcircuit_44_output, binary_cell_ram_subcircuit_43_output, binary_cell_ram_subcircuit_42_output, binary_cell_ram_subcircuit_41_output, binary_cell_ram_subcircuit_40_output, binary_cell_ram_subcircuit_39_output, binary_cell_ram_subcircuit_38_output, binary_cell_ram_subcircuit_37_output, binary_cell_ram_subcircuit_36_output, binary_cell_ram_subcircuit_35_output, binary_cell_ram_subcircuit_34_output, binary_cell_ram_subcircuit_33_output);
  Binary_cell___RAM_subcircuit binary_cell_ram_subcircuit_49 (
    .Input(I0), .Select(decoder_1_out0), .Read_Write(Read_Write),
    .Output(binary_cell_ram_subcircuit_49_output));
  Binary_cell___RAM_subcircuit binary_cell_ram_subcircuit_50 (
    .Input(I0), .Select(decoder_1_out1), .Read_Write(Read_Write),
    .Output(binary_cell_ram_subcircuit_50_output));
  Binary_cell___RAM_subcircuit binary_cell_ram_subcircuit_51 (
    .Input(I0), .Select(decoder_1_out2), .Read_Write(Read_Write),
    .Output(binary_cell_ram_subcircuit_51_output));
  Binary_cell___RAM_subcircuit binary_cell_ram_subcircuit_52 (
    .Input(I0), .Select(decoder_1_out3), .Read_Write(Read_Write),
    .Output(binary_cell_ram_subcircuit_52_output));
  Binary_cell___RAM_subcircuit binary_cell_ram_subcircuit_53 (
    .Input(I0), .Select(decoder_1_out4), .Read_Write(Read_Write),
    .Output(binary_cell_ram_subcircuit_53_output));
  Binary_cell___RAM_subcircuit binary_cell_ram_subcircuit_54 (
    .Input(I0), .Select(decoder_1_out5), .Read_Write(Read_Write),
    .Output(binary_cell_ram_subcircuit_54_output));
  Binary_cell___RAM_subcircuit binary_cell_ram_subcircuit_55 (
    .Input(I0), .Select(decoder_1_out6), .Read_Write(Read_Write),
    .Output(binary_cell_ram_subcircuit_55_output));
  Binary_cell___RAM_subcircuit binary_cell_ram_subcircuit_56 (
    .Input(I0), .Select(decoder_1_out7), .Read_Write(Read_Write),
    .Output(binary_cell_ram_subcircuit_56_output));
  Binary_cell___RAM_subcircuit binary_cell_ram_subcircuit_57 (
    .Input(I0), .Select(decoder_1_out8), .Read_Write(Read_Write),
    .Output(binary_cell_ram_subcircuit_57_output));
  Binary_cell___RAM_subcircuit binary_cell_ram_subcircuit_58 (
    .Input(I0), .Select(decoder_1_out9), .Read_Write(Read_Write),
    .Output(binary_cell_ram_subcircuit_58_output));
  Binary_cell___RAM_subcircuit binary_cell_ram_subcircuit_59 (
    .Input(I0), .Select(decoder_1_out10), .Read_Write(Read_Write),
    .Output(binary_cell_ram_subcircuit_59_output));
  Binary_cell___RAM_subcircuit binary_cell_ram_subcircuit_60 (
    .Input(I0), .Select(decoder_1_out11), .Read_Write(Read_Write),
    .Output(binary_cell_ram_subcircuit_60_output));
  Binary_cell___RAM_subcircuit binary_cell_ram_subcircuit_61 (
    .Input(I0), .Select(decoder_1_out12), .Read_Write(Read_Write),
    .Output(binary_cell_ram_subcircuit_61_output));
  Binary_cell___RAM_subcircuit binary_cell_ram_subcircuit_62 (
    .Input(I0), .Select(decoder_1_out13), .Read_Write(Read_Write),
    .Output(binary_cell_ram_subcircuit_62_output));
  Binary_cell___RAM_subcircuit binary_cell_ram_subcircuit_63 (
    .Input(I0), .Select(decoder_1_out14), .Read_Write(Read_Write),
    .Output(binary_cell_ram_subcircuit_63_output));
  Binary_cell___RAM_subcircuit binary_cell_ram_subcircuit_64 (
    .Input(I0), .Select(decoder_1_out15), .Read_Write(Read_Write),
    .Output(binary_cell_ram_subcircuit_64_output));
  or or_4 (O0, binary_cell_ram_subcircuit_64_output, binary_cell_ram_subcircuit_63_output, binary_cell_ram_subcircuit_62_output, binary_cell_ram_subcircuit_61_output, binary_cell_ram_subcircuit_60_output, binary_cell_ram_subcircuit_59_output, binary_cell_ram_subcircuit_58_output, binary_cell_ram_subcircuit_57_output, binary_cell_ram_subcircuit_56_output, binary_cell_ram_subcircuit_55_output, binary_cell_ram_subcircuit_54_output, binary_cell_ram_subcircuit_53_output, binary_cell_ram_subcircuit_52_output, binary_cell_ram_subcircuit_51_output, binary_cell_ram_subcircuit_50_output, binary_cell_ram_subcircuit_49_output);
endmodule

module DATA_PATH (
  input  Register___Write,
  input  [1:0] DA,
  input  [1:0] BA,
  input  [1:0] AA,
  input  User_Input_Select,
  input  Uin3,
  input  Uin2,
  input  Uin1,
  input  Uin0,
  input  RAM___Write_Read,
  input  S3,
  input  S2,
  input  S1,
  input  S0,
  input  ALU_RAM___select,
  output Cout,
  output G3,
  output G2,
  output G1,
  output G0
);

  wire alu_1_g0, alu_1_g1, alu_1_g2, alu_1_g3, n4x4_register_file_1_b0, n4x4_register_file_1_b1,
       n4x4_register_file_1_b2, n4x4_register_file_1_b3, n16x4_ram_1_o0, n16x4_ram_1_o1, n16x4_ram_1_o2,
       n16x4_ram_1_o3, quad_2x1_set_of_mux_1__01, quad_2x1_set_of_mux_1__02, quad_2x1_set_of_mux_1__03,
       quad_2x1_set_of_mux_1_o0;
  wire [3:0] n4x4_register_file_1_a0;

  Quad_2x1_Set_of_Mux quad_2x1_set_of_mux_1 (
    .A3(G3), .A2(G2), .A1(G1), .A0(G0), .L3(Uin3), .L2(Uin2), .L1(Uin1), .L0(Uin0), .S(User_Input_Select),
    ._03(quad_2x1_set_of_mux_1__03), ._02(quad_2x1_set_of_mux_1__02), ._01(quad_2x1_set_of_mux_1__01),
    .O0(quad_2x1_set_of_mux_1_o0));
  // Probe on n4x4_register_file_1_a0[3]
  // Probe on n4x4_register_file_1_b3
  // Probe on n4x4_register_file_1_a0[2]
  // Probe on n4x4_register_file_1_a0[1]
  // Probe on n4x4_register_file_1_a0[0]
  Quad_2x1_Set_of_Mux quad_2x1_set_of_mux_2 (
    .A3(alu_1_g3), .A2(alu_1_g2), .A1(alu_1_g1), .A0(alu_1_g0), .L3(n16x4_ram_1_o3), .L2(n16x4_ram_1_o2),
    .L1(n16x4_ram_1_o1), .L0(n16x4_ram_1_o0), .S(ALU_RAM___select), ._03(G3), ._02(G2), ._01(G1), .O0(G0));
  _4x4_register_File u_4x4_register_file_1 (
    .WRITE(Register___Write), .DA(DA), .AA(AA), .D3(quad_2x1_set_of_mux_1__03),
    .D2(quad_2x1_set_of_mux_1__02), .D1(quad_2x1_set_of_mux_1__01), .D0(quad_2x1_set_of_mux_1_o0),
    .A3(n4x4_register_file_1_a0[3]), .A2(n4x4_register_file_1_a0[2]), .A1(n4x4_register_file_1_a0[1]),
    .A0(n4x4_register_file_1_a0[0]), .B3(n4x4_register_file_1_b3), .B2(n4x4_register_file_1_b2),
    .B1(n4x4_register_file_1_b1), .B0(n4x4_register_file_1_b0), .BA(BA));
  // Probe on n4x4_register_file_1_b2
  // Probe on n4x4_register_file_1_b1
  // Probe on n4x4_register_file_1_b0
  ALU alu_1 (
    .X3(n4x4_register_file_1_a0[3]), .X2(n4x4_register_file_1_a0[2]), .X1(n4x4_register_file_1_a0[1]),
    .X0(n4x4_register_file_1_a0[0]), .Y3(n4x4_register_file_1_b3), .Y2(n4x4_register_file_1_b2),
    .Y1(n4x4_register_file_1_b1), .Y0(n4x4_register_file_1_b0), .S3(S3), .S2(S2), .S1(S1), .S0(S0),
    .Cout(Cout), .G3(alu_1_g3), .G2(alu_1_g2), .G1(alu_1_g1), .G0(alu_1_g0));
  _16x4_RAM u_16x4_ram_1 (
    .RAM_select(1'b1), .Address(n4x4_register_file_1_a0), .Read_Write(RAM___Write_Read),
    .I3(n4x4_register_file_1_b3), .I2(n4x4_register_file_1_b2), .I1(n4x4_register_file_1_b1),
    .I0(n4x4_register_file_1_b0), .O3(n16x4_ram_1_o3), .O2(n16x4_ram_1_o2), .O1(n16x4_ram_1_o1),
    .O0(n16x4_ram_1_o0));

  // Notes on the sheet:
  //   User Input Control
  //   4x4
  //   Register File
  //   ALU
  //   ALU / RAM - Input Control 
  //   RAM Address
  //   ALU 
  //   Output
  //   16x4 RAM
  //   RAM Input
  //   RAM Output
endmodule
