// Logisim project Q1 CIRCUIT.circ as structural Verilog: 1 circuit, main circuit main
module main (
  input  Y,
  input  Z,
  input  in_3,
  input  B,
  input  C,
  input  D,
  input  A,
  input  Y_2
);

  wire A_prime_D_out, AB_prime_out, and_1_out, BC_prime_out, CD_prime_out, not_1_out, not_2_out, not_3_out,
       not_4_out, not_5_out, not_6_out, or_1_out, or_2_out, or_3_out, X_prime_Y_out, XYZ_out, XYZ_prime_out;

  not not_1 (not_1_out, in_3);
  not not_2 (not_2_out, Y);
  LED led_1 (.in(Y_2));
  and XYZ (XYZ_out, Y, Z, in_3);
  and XYZ_prime (XYZ_prime_out, Y, Z, not_1_out);
  and X_prime_Y (X_prime_Y_out, not_2_out, Z);
  or or_1 (or_1_out, XYZ_out, XYZ_prime_out, X_prime_Y_out);
  LED led_2 (.in(or_1_out));
  not not_3 (not_3_out, C);
  not not_4 (not_4_out, D);
  not not_5 (not_5_out, A);
  not not_6 (not_6_out, B);
  and BC_prime (BC_prime_out, B, not_3_out);
  and CD_prime (CD_prime_out, C, not_4_out);
  and A_prime_D (A_prime_D_out, D, not_5_out);
  and AB_prime (AB_prime_out, A, not_6_out);
  or or_2 (or_2_out, BC_prime_out, A_prime_D_out);
  or or_3 (or_3_out, CD_prime_out, AB_prime_out);
  and and_1 (and_1_out, or_2_out, or_3_out);
  LED led_3 (.in(and_1_out));

  // Notes on the sheet:
  //   X
  //   UNSIMPLIFIED
  //   SIMPLIFIED
  //   BC' + A'D
  //   AB' + CD' 
endmodule
