// Logisim project Lab6 - circ.circ as structural Verilog: 1 circuit, main circuit main
module main (
  input  X,
  input  Y,
  input  Z
);

  wire and_1_out, and_2_out, and_3_out, or_1_out, xor_1_out, xor_2_out, xor_3_out;

  xor xor_1 (xor_1_out, Y, X);
  LED led_1 (.in(xor_1_out));
  LED led_2 (.in(and_1_out));
  and and_1 (and_1_out, Y, X);
  xor xor_2 (xor_2_out, X, Y);
  and and_2 (and_2_out, X, Y);
  xor xor_3 (xor_3_out, xor_2_out, Z);
  LED led_3 (.in(xor_3_out));
  and and_3 (and_3_out, xor_2_out, Z);
  or or_1 (or_1_out, and_3_out, and_2_out);
  LED led_4 (.in(or_1_out));

  // Notes on the sheet:
  //   C-HA
  //   S-HA
  //   X'Y + XY'
  //   XY
  //   S-FA
  //   XY' Z' + X'YZ' + X'Y'Z + XYZ
  //   C-FA
  //   XY + XY' Z + X'YZ
endmodule
