// Logisim project 231488347_lab9 circuit.circ as structural Verilog: 1 circuit, main circuit main
module main (
  input  [3:0] A,
  input  [3:0] B
);

  wire comparator_1_eq, comparator_1_gt, comparator_1_lt;

  LED led_1 (.in(comparator_1_gt));
  LED led_2 (.in(comparator_1_eq));
  Comparator #(.width(4)) comparator_1 (.a(A), .b(B), .gt(comparator_1_gt), .eq(comparator_1_eq), .lt(comparator_1_lt));
  LED led_3 (.in(comparator_1_lt));
endmodule
