# Fritzing sketch circuit (saved by Fritzing 0.9.6b)
breadboards: 1

parts:
  LED3 = LED - 3mm [color="Red (633nm)" current=0.030 package="3 mm [THT]"]
  LED4 = LED - 3mm [color="Red (633nm)" current=0.030 package="3 mm [THT]"]
  LED5 = LED - 3mm [color="Red (633nm)" current=0.030 package="3 mm [THT]"]
  LED6 = LED - 3mm [color="Red (633nm)" current=0.030 package="3 mm [THT]"]
  R2 = Resistor [tolerance=±5% power=0.25 resistance=220 package=THT]
  R3 = Resistor [tolerance=±5% power=0.25 resistance=220 package=THT]
  R4 = Resistor [tolerance=±5% power=0.25 resistance=220 package=THT]
  R1 = Resistor [tolerance=±5% power=0.25 resistance=220 package=THT]
  Part1 = Arduino Uno (Rev3)

nets:
  N1: LED3.cathode, R4.Pin_1
  N2: LED3.anode, LED4.anode, LED5.anode, LED6.anode, Part1.GND
  N3: LED4.cathode, R3.Pin_1
  N4: LED5.cathode, R2.Pin_1
  N5: LED6.cathode, R1.Pin_1
  N6: R2.Pin_0, Part1.D4
  N7: R3.Pin_0, Part1.D3_PWM
  N8: R4.Pin_0, Part1.D2
  N9: R1.Pin_0, Part1.D5_PWM
