# Fritzing sketch circuit (saved by Fritzing 0.9.10b)
breadboards: 1

parts:
  L298N1 = L298N DC motor driver
  M1 = DC Motor [voltage_(max)=6V voltage_(min)=3V]  # not connected
  HC-SR04_Sensor_1 = HC-SR04 Ultrasonic Distance Sensor
  Part1 = Arduino Uno (Rev3)

nets:
  5V: L298N1.5V, HC-SR04_Sensor_1.VCC, Part1.5V
  N1: L298N1.ENA, Part1.D9_PWM
  N2: L298N1.IN1, Part1.D7
  N3: L298N1.IN2, Part1.D6_PWM
  N4: HC-SR04_Sensor_1.TRIG, Part1.D3_PWM
  N5: HC-SR04_Sensor_1.ECHO, Part1.D2
  GND: HC-SR04_Sensor_1.GND, Part1.GND

custom parts:
  L298N DC motor driver: 2x DC motor driver with 78M05 positive voltage regulator (7..35 V) L298N: max 46 V, 2 A Set 5 V Enable jumper to enable 5 V regultor (needed for the L298N) and +5 V output at screw terminal or supply external +5 V at screw terminal Set ENA and/or ENB to +5 V to enable motor permanently or supply ENA and/or ENB with PWM signal IN1 and IN2 set rotation directory for motor A (OUT1/OUT2) IN2 and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
